// Digital circuit 6-Digit-Display.dig as structural Verilog
module _6_Digit_Display (
  input  [23:0] I,
  output [3:0] _0,
  output D0,
  output [3:0] _1,
  output D1,
  output [3:0] _2,
  output D2,
  output [3:0] _3,
  output D3,
  output [3:0] _4,
  output D4,
  output [3:0] _5,
  output D5
);


  assign _0 = I[23:20];
  assign _1 = I[19:16];
  assign _2 = I[15:12];
  assign _3 = I[11:8];
  assign _4 = I[7:4];
  assign _5 = I[3:0];
  assign D0 = 1'b0;
  assign D1 = 1'b0;
  assign D2 = 1'b0;
  assign D3 = 1'b0;
  assign D4 = 1'b0;
  assign D5 = 1'b0;
endmodule
