// Digital circuit 8-Digit-Display.dig as structural Verilog
module _8_Digit_Display (
  input  [31:0] I,
  output [3:0] _0,
  output D0,
  output [3:0] _1,
  output D1,
  output [3:0] _2,
  output D2,
  output [3:0] _3,
  output D3,
  output [3:0] _4,
  output D4,
  output [3:0] _5,
  output D5,
  output [3:0] _6,
  output D6,
  output [3:0] _7,
  output D7
);


  assign _0 = I[31:28];
  assign _1 = I[27:24];
  assign _2 = I[23:20];
  assign _3 = I[19:16];
  assign _4 = I[15:12];
  assign _5 = I[11:8];
  assign _6 = I[7:4];
  assign _7 = I[3:0];
  assign D0 = 1'b0;
  assign D1 = 1'b0;
  assign D2 = 1'b0;
  assign D3 = 1'b0;
  assign D4 = 1'b0;
  assign D5 = 1'b0;
  assign D6 = 1'b0;
  assign D7 = 1'b0;
endmodule
