// Digital circuit Binary-BCD-Converter.dig as structural Verilog
module Binary_BCD_Converter (
  input  [4:0] I,
  output [3:0] _0,
  output D0,
  output [3:0] _1,
  output D1
);

  wire and_1_out, and_2_out, and_3_out, and_4_out, and_5_out, and_6_out, and_7_out, and_8_out, and_9_out,
       and_10_out, and_11_out, and_12_out, and_13_out, and_14_out, and_15_out, and_16_out, and_17_out,
       and_18_out;

  and and_1 (and_1_out, I[1], ~I[3], ~I[4]);  // And
  and and_2 (and_2_out, ~I[1], I[2], I[3], ~I[4]);  // And
  and and_3 (and_3_out, I[1], ~I[2], I[3], I[4]);  // And
  and and_4 (and_4_out, ~I[1], ~I[2], ~I[3], I[4]);  // And
  and and_5 (and_5_out, I[1], I[2], ~I[3]);  // And
  and and_6 (and_6_out, I[2], ~I[3], ~I[4]);  // And
  and and_7 (and_7_out, I[1], I[2], ~I[4]);  // And
  and and_8 (and_8_out, ~I[2], I[3], I[4]);  // And
  and and_9 (and_9_out, ~I[1], ~I[2], I[4]);  // And
  and and_10 (and_10_out, ~I[1], ~I[2], I[3], ~I[4]);  // And
  and and_11 (and_11_out, ~I[1], I[2], I[3], I[4]);  // And
  and and_12 (and_12_out, I[1], ~I[2], ~I[3], I[4]);  // And
  and and_13 (and_13_out, I[1], I[3], ~I[4]);  // And
  and and_14 (and_14_out, I[2], I[3], ~I[4]);  // And
  and and_15 (and_15_out, I[1], I[2], I[3]);
  and and_16 (and_16_out, ~I[2], ~I[3], I[4]);  // And
  and and_17 (and_17_out, I[3], I[4]);
  and and_18 (and_18_out, I[2], I[4]);
  or or_1 (_1[1], and_1_out, and_2_out, and_3_out, and_4_out, and_5_out);
  or or_2 (_1[2], and_6_out, and_7_out, and_8_out, and_9_out);
  or or_3 (_1[3], and_10_out, and_11_out, and_12_out);
  or or_4 (_0[0], and_13_out, and_14_out, and_15_out, and_16_out);
  or or_5 (_0[1], and_17_out, and_18_out);

  assign _0[3:2] = 2'b00;
  assign _1[0] = I[0];
  assign D0 = 1'b0;
  assign D1 = 1'b0;
endmodule
