// Digital circuit FFmodetest.dig as structural Verilog
module FFmodetest (
  input  clk
);

  wire counter_1_ovf;
  wire [7:0] counter_1_out;

  Counter #(.Bits(8)) counter_1 (.en(1'b1), .C(clk), .clr(1'b0), .out(counter_1_out), .ovf(counter_1_ovf));
  Break break_1 (.brk(counter_1_ovf));
endmodule
