// Digital circuit RV32I-ALU-Input-Instruction-Decoder.dig as structural Verilog
module RV32I_ALU_Input_Instruction_Decoder (
  input  [31:0] IN,
  output [5:0] FORMAT,
  output [2:0] ALU_A_SOURCE,
  output [1:0] ALU_B_SOURCE
);

  wire and_2_out, and_3_out, and_4_out, and_7_out, and_8_out, and_10_out, and_11_out, and_12_out, and_13_out,
       and_14_out;

  and and_1 (FORMAT[0], ~IN[2], ~IN[3], IN[4], IN[5], ~IN[6]);  // And
  and and_2 (and_2_out, IN[2], IN[3], ~IN[4], ~IN[5], IN[6]);  // And
  and and_3 (and_3_out, ~IN[2], ~IN[3], ~IN[4], ~IN[5], ~IN[6]);  // And
  and and_4 (and_4_out, ~IN[2], ~IN[3], IN[4], ~IN[5], ~IN[6]);  // And
  and and_5 (FORMAT[2], ~IN[2], ~IN[3], ~IN[4], IN[5], ~IN[6]);  // And
  and and_6 (FORMAT[3], ~IN[2], ~IN[3], ~IN[4], IN[5], IN[6]);  // And
  and and_7 (and_7_out, IN[2], ~IN[3], IN[4], IN[5], ~IN[6]);  // And
  and and_8 (and_8_out, IN[2], ~IN[3], IN[4], ~IN[5], ~IN[6]);  // And
  and and_9 (FORMAT[5], IN[2], IN[3], ~IN[4], IN[5], IN[6]);  // And
  and and_10 (and_10_out, ~IN[2], ~IN[3], ~IN[6]);  // And
  and and_11 (and_11_out, IN[2], ~IN[3], ~IN[4], IN[5], IN[6]);  // And
  and and_12 (and_12_out, ~IN[2], ~IN[3], ~IN[4], IN[5], IN[6]);  // And
  and and_13 (and_13_out, IN[2], IN[3], ~IN[4], IN[5], IN[6]);  // And
  and and_14 (and_14_out, IN[2], ~IN[3], IN[4], ~IN[5], ~IN[6]);  // And
  and and_15 (ALU_A_SOURCE[2], IN[2], ~IN[3], IN[4], IN[5], ~IN[6]);  // And
  nand nand_1 (ALU_B_SOURCE[0], ~IN[2], ~IN[3], IN[4], IN[5], ~IN[6]);  // NAnd
  and and_16 (ALU_B_SOURCE[1], ~IN[2], ~IN[3], IN[4], IN[5], ~IN[6]);  // And
  or or_1 (FORMAT[1], and_2_out, and_3_out, and_4_out);
  or or_2 (FORMAT[4], and_7_out, and_8_out);
  or or_3 (ALU_A_SOURCE[0], and_10_out, and_11_out);
  or or_4 (ALU_A_SOURCE[1], and_12_out, and_13_out, and_14_out);

  // Notes on the sheet:
  //   IN: default 20191123
endmodule
