// Digital circuit RV32I-ALU.dig as structural Verilog
module RV32I_ALU (
  input  [31:0] A,
  input  [31:0] B,
  input  [3:0] O,
  input  [5:0] S,
  output [31:0] Y,
  output [2:0] SO
);

  wire A___B, A__plus__B, AND, OR, PASS_A, PASS_B, SLL, SRA, SRL, XOR;
  wire [31:0] ADD_s, and_1_out, or_1_out, SLL_out, SRA_out, SRL_out, SUB_s, xor_1_out;

  Add #(.Bits(32)) ADD (.a(A), .b(B), .c_i(1'b0), .s(ADD_s));  // open: c_o
  Add #(.Bits(32)) SUB (.a(A), .b(B), .c_i(1'b0), .s(SUB_s));  // open: c_o
  assign and_1_out = A & B;  // And and_1, 32 bits wide
  assign or_1_out = A | B;  // Or or_1, 32 bits wide
  assign xor_1_out = A ^ B;  // XOr xor_1, 32 bits wide
  BarrelShifter #(.Bits(32)) u_SLL (.in(A), .shift(S), .out(SLL_out));
  BarrelShifter #(.Bits(32), .direction("right")) u_SRL (.in(A), .shift(S), .out(SRL_out));
  BarrelShifter #(.Bits(32), .barrelShifterMode("arithmetic"), .direction("right")) u_SRA (
    .in(A), .shift(S), .out(SRA_out));
  Comparator #(.Signed("true"), .Bits(32)) COMP (.a(A), .b(B), .eq(SO[0]), .lt(SO[1]));  // open: gt
  Comparator #(.Bits(32)) COMP_U (.a(A), .b(B), .eq(SO[0]), .lt(SO[2]));  // open: gt
  Decoder #(.Selector_Bits(4)) decoder_1 (
    .sel(O), .out_0(PASS_A), .out_1(A__plus__B), .out_2(AND), .out_3(SLL), .out_6(OR), .out_7(SRL),
    .out_8(PASS_B), .out_9(A___B), .out_14(XOR), .out_15(SRA));  // open: out_4, out_5, out_10, out_11, out_12, out_13
  assign Y = PASS_A ? A : 32'bz;  // Driver driver_1
  assign Y = PASS_B ? B : 32'bz;  // Driver driver_2
  assign Y = A__plus__B ? ADD_s : 32'bz;  // Driver driver_3
  assign Y = A___B ? SUB_s : 32'bz;  // Driver driver_4
  assign Y = AND ? and_1_out : 32'bz;  // Driver driver_5
  assign Y = OR ? or_1_out : 32'bz;  // Driver driver_6
  assign Y = XOR ? xor_1_out : 32'bz;  // Driver driver_7
  assign Y = SLL ? SLL_out : 32'bz;  // Driver driver_8
  assign Y = SRL ? SRL_out : 32'bz;  // Driver driver_9
  assign Y = SRA ? SRA_out : 32'bz;  // Driver driver_10
endmodule
