// Digital circuit RV32I-Branch-Hold.dig as structural Verilog
module RV32I_Branch_Hold (
  input  [31:0] I,
  output H
);

  wire [31:0] sub_1_s;

  Sub #(.Bits(32)) sub_1 (.a(32'h1000), .b(32'h15000), .c_i(1'b1), .s(sub_1_s));  // open: c_o
  and and_1 (H, ~I[4], I[5], I[6]);  // And
endmodule
