// Digital circuit RV32I-Comparator.dig as structural Verilog
module RV32I_Comparator (
  input  [31:0] A,
  input  [31:0] B,
  input  [7:0] SEL,
  output Y
);

  wire [7:0] and_1_out, not_1_out;

  Comparator #(.Signed("true"), .Bits(32)) COMP (.a(A), .b(B), .eq(not_1_out[0]), .lt(not_1_out[4]));  // open: gt
  Comparator #(.Bits(32)) COMP_U (.a(A), .b(B), .lt(not_1_out[6]));  // open: gt, eq
  not not_1 (not_1_out[1], not_1_out[0]);
  not not_2 (not_1_out[5], not_1_out[4]);
  not not_3 (not_1_out[7], not_1_out[6]);
  assign and_1_out = {not_1_out[7:4], not_1_out[6], not_1_out[4], not_1_out[1:0]} & SEL;  // And and_1, 8 bits wide
  or or_1 (Y, and_1_out[0], and_1_out[1], and_1_out[2], and_1_out[3], and_1_out[4], and_1_out[5], and_1_out[6], and_1_out[7]);
endmodule
