// Digital circuit RV32I-Control.dig as structural Verilog
module RV32I_Control (
  input  START,
  input  PAUSE,
  input  RESET,
  input  HOLD,
  input  SET_ERROR,
  input  BC,
  input  BCO,
  input  CLC,
  input  RUN_OVERRIDE,
  output NORMAL,
  output RUN,
  output GO,
  output ERROR,
  output BCE,
  output BC_SET_R_W_A,
  output ROM_SET_MEM_R_W
);

  wire and_1_out, and_2_out, and_3_out, HOLD_GO_q, jk_ff_1_nq, nand_1_out, or_1_out, or_2_out, Pause_Run_q;

  JK_FF jk_ff_1 (.J(START), .C(CLC), .K(~START), .nQ(jk_ff_1_nq));  // open: Q
  and and_1 (and_1_out, START, jk_ff_1_nq);
  or or_1 (or_1_out, BC, BCO, NORMAL);
  or or_2 (or_2_out, and_1_out, RUN);
  and and_2 (and_2_out, or_1_out, ~RESET);  // And
  and and_3 (and_3_out, ~BCO, or_2_out, ~PAUSE, ~BC);  // And
  nand nand_1 (nand_1_out, 1'b1, RUN, NORMAL);
  D_FF Boot_Normal (.D(and_2_out), .C(CLC), .Q(NORMAL), .nQ(BC_SET_R_W_A));
  D_FF #(.Default(1)) Pause_Run (.D(and_3_out), .C(CLC), .Q(Pause_Run_q));  // open: nQ
  D_FF #(.Default(1)) HOLD_GO (.D(nand_1_out), .C(CLC), .Q(HOLD_GO_q));  // open: nQ
  or or_3 (RUN, Pause_Run_q, RUN_OVERRIDE);
  not not_1 (GO, HOLD);
  and and_4 (BCE, BC_SET_R_W_A, RUN);

  assign ERROR = SET_ERROR;
  assign ROM_SET_MEM_R_W = BC_SET_R_W_A;

  // Notes on the sheet:
  //   STATUS
endmodule
