// Digital circuit RV32I-Decode-Control.dig as structural Verilog
module RV32I_Decode_Control (
  input  [31:0] INSTR,
  input  Normal,
  input  Run,
  input  Go,
  output DECODE_HOLD,
  output DECODE_EN,
  output WRITE_RD,
  output READ_RS1,
  output READ_RS2,
  output ERROR
);

  wire rv32i_decode_instruction_decoder_1_e, rv32i_decode_instruction_decoder_1_rd,
       rv32i_decode_instruction_decoder_1_rs1, rv32i_decode_instruction_decoder_1_rs2;

  RV32I_Decode_Instruction_Decoder rv32i_decode_instruction_decoder_1 (
    .IN(INSTR), .RD(rv32i_decode_instruction_decoder_1_rd), .RS1(rv32i_decode_instruction_decoder_1_rs1),
    .RS2(rv32i_decode_instruction_decoder_1_rs2), .E(rv32i_decode_instruction_decoder_1_e));
  and and_1 (DECODE_HOLD, ~INSTR[4], INSTR[5], INSTR[6]);  // And
  and and_2 (DECODE_EN, Normal, Run);
  and and_3 (WRITE_RD, rv32i_decode_instruction_decoder_1_rd, Normal, Run);
  and and_4 (READ_RS1, rv32i_decode_instruction_decoder_1_rs1, Normal, Run);
  and and_5 (READ_RS2, rv32i_decode_instruction_decoder_1_rs2, Normal, Run);
  and and_6 (ERROR, rv32i_decode_instruction_decoder_1_e, Run, Normal, Go);
endmodule
