// Digital circuit RV32I-Decode-Instruction-Decoder.dig as structural Verilog
module RV32I_Decode_Instruction_Decoder (
  input  [31:0] IN,
  output RD,
  output RS1,
  output RS2,
  output E
);

  wire and_1_out, and_2_out, and_3_out, and_4_out, and_5_out, and_6_out, and_7_out, and_8_out, and_9_out,
       and_10_out, and_11_out, and_12_out, and_13_out, and_14_out, and_15_out, and_16_out, and_17_out,
       and_18_out, and_19_out, and_20_out, and_21_out, and_22_out, and_23_out, and_24_out, and_25_out,
       and_26_out, and_27_out, and_28_out, and_29_out, and_30_out, and_31_out, and_32_out, and_33_out,
       and_34_out, and_35_out, and_36_out, and_37_out, and_38_out, and_39_out, and_40_out, and_41_out;

  nand nand_1 (RD, ~IN[2], ~IN[3], ~IN[4], IN[5]);  // NAnd
  and and_1 (and_1_out, IN[2], ~IN[3], IN[4], ~IN[6]);  // And
  and and_2 (and_2_out, IN[2], IN[3], ~IN[4], IN[5], IN[6]);  // And
  and and_3 (and_3_out, ~IN[2], ~IN[3], IN[4], IN[5], ~IN[6]);  // And
  and and_4 (and_4_out, ~IN[2], ~IN[3], ~IN[4], IN[5]);  // And
  and and_5 (and_5_out, IN[0], IN[1], ~IN[2], ~IN[3], IN[4], IN[5], ~IN[6], ~IN[12], ~IN[13], ~IN[14], ~IN[25], ~IN[26], ~IN[27], ~IN[28], ~IN[29], ~IN[30], ~IN[31]);  // And
  and and_6 (and_6_out, IN[0], IN[1], ~IN[2], ~IN[3], IN[4], IN[5], ~IN[6], ~IN[12], ~IN[13], ~IN[14], ~IN[25], ~IN[26], ~IN[27], ~IN[28], ~IN[29], IN[30], ~IN[31]);  // And
  and and_7 (and_7_out, IN[0], IN[1], ~IN[2], ~IN[3], IN[4], IN[5], ~IN[6], IN[12], IN[13], IN[14], ~IN[25], ~IN[26], ~IN[27], ~IN[28], ~IN[29], ~IN[30], ~IN[31]);  // And
  and and_8 (and_8_out, IN[0], IN[1], ~IN[2], ~IN[3], IN[4], IN[5], ~IN[6], ~IN[12], IN[13], IN[14], ~IN[25], ~IN[26], ~IN[27], ~IN[28], ~IN[29], ~IN[30], ~IN[31]);  // And
  and and_9 (and_9_out, IN[0], IN[1], ~IN[2], ~IN[3], IN[4], IN[5], ~IN[6], ~IN[12], ~IN[13], IN[14], ~IN[25], ~IN[26], ~IN[27], ~IN[28], ~IN[29], ~IN[30], ~IN[31]);  // And
  and and_10 (and_10_out, IN[0], IN[1], ~IN[2], ~IN[3], IN[4], ~IN[5], ~IN[6], ~IN[12], ~IN[13], ~IN[14]);  // And
  and and_11 (and_11_out, IN[0], IN[1], ~IN[2], ~IN[3], IN[4], ~IN[5], ~IN[6], IN[12], IN[13], IN[14]);  // And
  and and_12 (and_12_out, IN[0], IN[1], ~IN[2], ~IN[3], IN[4], ~IN[5], ~IN[6], ~IN[12], IN[13], IN[14]);  // And
  and and_13 (and_13_out, IN[0], IN[1], ~IN[2], ~IN[3], IN[4], ~IN[5], ~IN[6], ~IN[12], ~IN[13], IN[14]);  // And
  and and_14 (and_14_out, IN[0], IN[1], ~IN[2], ~IN[3], IN[4], IN[5], ~IN[6], IN[12], ~IN[13], ~IN[14], ~IN[25], ~IN[26], ~IN[27], ~IN[28], ~IN[29], ~IN[30], ~IN[31]);  // And
  and and_15 (and_15_out, IN[0], IN[1], ~IN[2], ~IN[3], IN[4], IN[5], ~IN[6], IN[12], ~IN[13], IN[14], ~IN[25], ~IN[26], ~IN[27], ~IN[28], ~IN[29], ~IN[30], ~IN[31]);  // And
  and and_16 (and_16_out, IN[0], IN[1], ~IN[2], ~IN[3], IN[4], IN[5], ~IN[6], IN[12], ~IN[13], IN[14], ~IN[25], ~IN[26], ~IN[27], ~IN[28], ~IN[29], IN[30], ~IN[31]);  // And
  and and_17 (and_17_out, IN[0], IN[1], ~IN[2], ~IN[3], IN[4], ~IN[5], ~IN[6], IN[12], ~IN[13], ~IN[14], ~IN[25], ~IN[26], ~IN[27], ~IN[28], ~IN[29], ~IN[30], ~IN[31]);  // And
  and and_18 (and_18_out, IN[0], IN[1], ~IN[2], ~IN[3], IN[4], ~IN[5], ~IN[6], IN[12], ~IN[13], IN[14], ~IN[25], ~IN[26], ~IN[27], ~IN[28], ~IN[29], ~IN[30], ~IN[31]);  // And
  and and_19 (and_19_out, IN[0], IN[1], ~IN[2], ~IN[3], IN[4], ~IN[5], ~IN[6], IN[12], ~IN[13], IN[14], ~IN[25], ~IN[26], ~IN[27], ~IN[28], ~IN[29], IN[30], ~IN[31]);  // And
  and and_20 (and_20_out, IN[0], IN[1], ~IN[2], ~IN[3], IN[4], IN[5], ~IN[6], ~IN[12], IN[13], ~IN[14], ~IN[25], ~IN[26], ~IN[27], ~IN[28], ~IN[29], ~IN[30], ~IN[31]);  // And
  and and_21 (and_21_out, IN[0], IN[1], ~IN[2], ~IN[3], IN[4], IN[5], ~IN[6], IN[12], IN[13], ~IN[14], ~IN[25], ~IN[26], ~IN[27], ~IN[28], ~IN[29], ~IN[30], ~IN[31]);  // And
  and and_22 (and_22_out, IN[0], IN[1], ~IN[2], ~IN[3], IN[4], ~IN[5], ~IN[6], ~IN[12], IN[13], ~IN[14]);  // And
  and and_23 (and_23_out, IN[0], IN[1], ~IN[2], ~IN[3], IN[4], ~IN[5], ~IN[6], IN[12], IN[13], ~IN[14]);  // And
  and and_24 (and_24_out, IN[0], IN[1], IN[2], ~IN[3], IN[4], IN[5], ~IN[6]);  // And
  and and_25 (and_25_out, IN[0], IN[1], IN[2], ~IN[3], IN[4], ~IN[5], ~IN[6]);  // And
  and and_26 (and_26_out, IN[0], IN[1], IN[2], IN[3], ~IN[4], IN[5], IN[6]);  // And
  and and_27 (and_27_out, IN[0], IN[1], IN[2], ~IN[3], ~IN[4], IN[5], IN[6], ~IN[12], ~IN[13], ~IN[14]);  // And
  and and_28 (and_28_out, IN[0], IN[1], ~IN[2], ~IN[3], ~IN[4], IN[5], IN[6], ~IN[12], ~IN[13], ~IN[14]);  // And
  and and_29 (and_29_out, IN[0], IN[1], ~IN[2], ~IN[3], ~IN[4], IN[5], IN[6], IN[12], ~IN[13], ~IN[14]);  // And
  and and_30 (and_30_out, IN[0], IN[1], ~IN[2], ~IN[3], ~IN[4], IN[5], IN[6], ~IN[12], ~IN[13], IN[14]);  // And
  and and_31 (and_31_out, IN[0], IN[1], ~IN[2], ~IN[3], ~IN[4], IN[5], IN[6], IN[12], ~IN[13], IN[14]);  // And
  and and_32 (and_32_out, IN[0], IN[1], ~IN[2], ~IN[3], ~IN[4], IN[5], IN[6], ~IN[12], IN[13], IN[14]);  // And
  and and_33 (and_33_out, IN[0], IN[1], ~IN[2], ~IN[3], ~IN[4], IN[5], IN[6], IN[12], IN[13], IN[14]);  // And
  and and_34 (and_34_out, IN[0], IN[1], ~IN[2], ~IN[3], ~IN[4], ~IN[5], ~IN[6], ~IN[12], ~IN[13], ~IN[14]);  // And
  and and_35 (and_35_out, IN[0], IN[1], ~IN[2], ~IN[3], ~IN[4], ~IN[5], ~IN[6], IN[12], ~IN[13], ~IN[14]);  // And
  and and_36 (and_36_out, IN[0], IN[1], ~IN[2], ~IN[3], ~IN[4], ~IN[5], ~IN[6], ~IN[12], IN[13], ~IN[14]);  // And
  and and_37 (and_37_out, IN[0], IN[1], ~IN[2], ~IN[3], ~IN[4], ~IN[5], ~IN[6], ~IN[12], ~IN[13], IN[14]);  // And
  and and_38 (and_38_out, IN[0], IN[1], ~IN[2], ~IN[3], ~IN[4], ~IN[5], ~IN[6], IN[12], ~IN[13], IN[14]);  // And
  and and_39 (and_39_out, IN[0], IN[1], ~IN[2], ~IN[3], ~IN[4], IN[5], ~IN[6], ~IN[12], ~IN[13], ~IN[14]);  // And
  and and_40 (and_40_out, IN[0], IN[1], ~IN[2], ~IN[3], ~IN[4], IN[5], ~IN[6], IN[12], ~IN[13], ~IN[14]);  // And
  and and_41 (and_41_out, IN[0], IN[1], ~IN[2], ~IN[3], ~IN[4], IN[5], ~IN[6], ~IN[12], IN[13], ~IN[14]);  // And
  nor nor_1 (RS1, and_1_out, and_2_out);
  or or_1 (RS2, and_3_out, and_4_out);
  nor nor_2 (E, and_5_out, and_6_out, and_7_out, and_8_out, and_9_out, and_10_out, and_11_out, and_12_out, and_13_out, and_14_out, and_15_out, and_16_out, and_17_out, and_18_out, and_19_out, and_20_out, and_21_out, and_22_out, and_23_out, and_24_out, and_25_out, and_26_out, and_27_out, and_28_out, and_29_out, and_30_out, and_31_out, and_32_out, and_33_out, and_34_out, and_35_out, and_36_out, and_37_out, and_38_out, and_39_out, and_40_out, and_41_out);

  // Notes on the sheet:
  //   IN: default 20191123
  //   Write to Register
  //   ADD
  //   SUB
  //   AND
  //   OR
  //   XOR
  //   ADDI
  //   ANDI
  //   ORI
  //   XORI
  //   SLL
  //   SRL
  //   SRA
  //   SLLI
  //   SRLI
  //   SRAI
  //   SLT
  //   SLTU
  //   SLTI
  //   SLTIU
  //   LUI
  //   AUIPC
  //   JAL
  //   JALR
  //   BEQ
  //   BNE
  //   BLT
  //   BGE
  //   BLTU
  //   BGEU
  //   LB
  //   LH
  //   LW
  //   LBU
  //   LHU
  //   SB
  //   SH
  //   SW
endmodule
