// Digital circuit RV32I-Execute-Control.dig as structural Verilog
module RV32I_Execute_Control (
  input  [31:0] INSTR,
  input  Normal,
  input  Run,
  input  Go,
  output DECODE_HOLD,
  output DECODE_EN,
  output RESERVE,
  output ERROR
);

  wire nor_1_out, rv32i_instruction_decoder_1_e;
  wire [36:0] rv32i_instruction_decoder_1_i;

  RV32I_Instruction_Decoder rv32i_instruction_decoder_1 (
    .IN(INSTR), .I(rv32i_instruction_decoder_1_i), .E(rv32i_instruction_decoder_1_e));
  or or_1 (DECODE_HOLD, rv32i_instruction_decoder_1_i[21], rv32i_instruction_decoder_1_i[22], rv32i_instruction_decoder_1_i[23], rv32i_instruction_decoder_1_i[24], rv32i_instruction_decoder_1_i[25], rv32i_instruction_decoder_1_i[26], rv32i_instruction_decoder_1_i[27], rv32i_instruction_decoder_1_i[28]);
  nor nor_1 (nor_1_out, rv32i_instruction_decoder_1_i[23], rv32i_instruction_decoder_1_i[24], rv32i_instruction_decoder_1_i[25], rv32i_instruction_decoder_1_i[26], rv32i_instruction_decoder_1_i[27], rv32i_instruction_decoder_1_i[28], rv32i_instruction_decoder_1_i[34], rv32i_instruction_decoder_1_i[35], rv32i_instruction_decoder_1_i[36]);
  and and_1 (ERROR, rv32i_instruction_decoder_1_e, Run, Normal, Go);
  and and_2 (DECODE_EN, Normal, Run);
  and and_3 (RESERVE, nor_1_out, Normal, Run, Go);
endmodule
