// Digital circuit RV32I-Execute-Instruction-Decoder.dig as structural Verilog
module RV32I_Execute_Instruction_Decoder (
  input  [31:0] IN,
  output [7:0] ALU_INSTR,
  output [7:0] COMP_SEL,
  output [1:0] JUMP
);

  wire and_1_out, and_2_out, and_3_out, and_4_out, nand_1_out;

  and and_1 (and_1_out, ~IN[2], ~IN[3], IN[4], ~IN[6], ~IN[12], IN[13], ~IN[14]);  // And
  and and_2 (and_2_out, ~IN[2], ~IN[3], IN[4], ~IN[6], IN[12], IN[13], ~IN[14]);  // And
  nand nand_1 (nand_1_out, ~IN[2], ~IN[3], IN[4], ~IN[6]);  // NAnd
  and and_3 (and_3_out, ~IN[2], ~IN[3], IN[4], IN[5], ~IN[6], ~IN[12], ~IN[13], ~IN[14], ~IN[30]);  // And
  and and_4 (and_4_out, ~IN[2], ~IN[3], IN[4], ~IN[5], ~IN[6], ~IN[12], ~IN[13], ~IN[14]);  // And
  and and_5 (ALU_INSTR[1], ~IN[2], ~IN[3], IN[4], ~IN[6], ~IN[12], IN[13], IN[14]);  // And
  and and_6 (ALU_INSTR[2], ~IN[2], ~IN[3], IN[4], ~IN[6], IN[12], IN[13], IN[14]);  // And
  and and_7 (ALU_INSTR[3], ~IN[2], ~IN[3], IN[4], ~IN[6], IN[12], ~IN[13], IN[14], ~IN[30]);  // And
  and and_8 (ALU_INSTR[4], ~IN[2], ~IN[3], IN[4], IN[5], ~IN[6], ~IN[12], ~IN[13], ~IN[14], IN[30]);  // And
  and and_9 (ALU_INSTR[5], ~IN[2], ~IN[3], IN[4], ~IN[6], ~IN[12], ~IN[13], IN[14]);  // And
  and and_10 (ALU_INSTR[6], ~IN[2], ~IN[3], IN[4], ~IN[6], IN[12], ~IN[13], ~IN[14]);  // And
  and and_11 (ALU_INSTR[7], ~IN[2], ~IN[3], IN[4], ~IN[6], IN[12], ~IN[13], IN[14], IN[30]);  // And
  and and_12 (COMP_SEL[0], ~IN[12], ~IN[13], ~IN[14]);  // And
  and and_13 (COMP_SEL[1], IN[12], ~IN[13], ~IN[14]);  // And
  and and_14 (COMP_SEL[2], ~IN[12], IN[13], ~IN[14]);  // And
  and and_15 (COMP_SEL[3], IN[12], IN[13], ~IN[14]);  // And
  and and_16 (COMP_SEL[4], ~IN[12], ~IN[13], IN[14]);  // And
  and and_17 (COMP_SEL[5], IN[12], ~IN[13], IN[14]);  // And
  and and_18 (COMP_SEL[6], ~IN[12], IN[13], IN[14]);  // And
  and and_19 (COMP_SEL[7], IN[12], IN[13], IN[14]);
  and and_20 (JUMP[0], IN[2], ~IN[4], IN[5], IN[6]);  // And
  and and_21 (JUMP[1], ~IN[2], ~IN[3], ~IN[4], IN[5], IN[6]);  // And
  or or_1 (ALU_INSTR[0], and_1_out, and_2_out, nand_1_out, and_3_out, and_4_out);

  // Notes on the sheet:
  //   IN: default 20191123
  //   SLT
  //   SLTU
  //   OTHER
  //   ADD
  //   ADDI
  //   OR
  //   AND
  //   SRL
  //   SUB
  //   XOR
  //   SLL
  //   SRA
endmodule
