// Digital circuit RV32I-Fetch-Control.dig as structural Verilog
module RV32I_Fetch_Control (
  input  Normal,
  input  Run,
  input  Go,
  input  ALU_SET_PC,
  input  WRITE_TO_MEMORY,
  output PC_EN,
  output PC_INC_SET_PC,
  output PC_STALL,
  output MEM_STR
);

  or or_1 (MEM_STR, WRITE_TO_MEMORY, ~Normal);  // Or
  and and_1 (PC_EN, Normal, Run);
  and and_2 (PC_INC_SET_PC, Go, ~ALU_SET_PC);  // And
  and and_3 (PC_STALL, ~Go, ~ALU_SET_PC);  // And
endmodule
