// Digital circuit RV32I-Instruction-Decoder.dig as structural Verilog
module RV32I_Instruction_Decoder (
  input  [31:0] IN,
  output BRANCH_HOLD,
  output REG_HOLD,
  output [5:0] FORMAT,
  output [2:0] ALU_A_SOURCE,
  output [1:0] ALU_B_SOURCE,
  output RESULT_IS_COMP,
  output [3:0] EXECUTE_RESULT_DESTINATION,
  output [7:0] ALU_INSTR,
  output [7:0] COMP_SEL,
  output [7:0] MEMORY_ACCESS,
  output E
);

  wire and_3_out, and_4_out, and_5_out, and_8_out, and_9_out, and_11_out, and_12_out, and_13_out, and_14_out,
       and_15_out, and_18_out, and_19_out, and_20_out, and_21_out, and_44_out, and_45_out, and_46_out,
       and_47_out, and_48_out, and_49_out, and_50_out, and_51_out, and_52_out, and_53_out, and_54_out,
       and_55_out, and_56_out, and_57_out, and_58_out, and_59_out, and_60_out, and_61_out, and_62_out,
       and_63_out, and_64_out, and_65_out, and_66_out, and_67_out, and_68_out, and_69_out, and_70_out,
       and_71_out, and_72_out, and_73_out, and_74_out, and_75_out, and_76_out, and_77_out, and_78_out,
       and_79_out, and_80_out, nand_3_out;

  and and_1 (BRANCH_HOLD, ~IN[4], IN[5], IN[6]);  // And
  nand nand_1 (REG_HOLD, ~IN[2], ~IN[3], ~IN[4], IN[5]);  // NAnd
  and and_2 (FORMAT[0], ~IN[2], ~IN[3], IN[4], IN[5], ~IN[6]);  // And
  and and_3 (and_3_out, IN[2], IN[3], ~IN[4], ~IN[5], IN[6]);  // And
  and and_4 (and_4_out, ~IN[2], ~IN[3], ~IN[4], ~IN[5], ~IN[6]);  // And
  and and_5 (and_5_out, ~IN[2], ~IN[3], IN[4], ~IN[5], ~IN[6]);  // And
  and and_6 (FORMAT[2], ~IN[2], ~IN[3], ~IN[4], IN[5], ~IN[6]);  // And
  and and_7 (FORMAT[3], ~IN[2], ~IN[3], ~IN[4], IN[5], IN[6]);  // And
  and and_8 (and_8_out, IN[2], ~IN[3], IN[4], IN[5], ~IN[6]);  // And
  and and_9 (and_9_out, IN[2], ~IN[3], IN[4], ~IN[5], ~IN[6]);  // And
  and and_10 (FORMAT[5], IN[2], IN[3], ~IN[4], IN[5], IN[6]);  // And
  and and_11 (and_11_out, ~IN[2], ~IN[3], ~IN[6]);  // And
  and and_12 (and_12_out, IN[2], ~IN[3], ~IN[4], IN[5], IN[6]);  // And
  and and_13 (and_13_out, ~IN[2], ~IN[3], ~IN[4], IN[5], IN[6]);  // And
  and and_14 (and_14_out, IN[2], IN[3], ~IN[4], IN[5], IN[6]);  // And
  and and_15 (and_15_out, IN[2], ~IN[3], IN[4], ~IN[5], ~IN[6]);  // And
  and and_16 (ALU_A_SOURCE[2], IN[2], ~IN[3], IN[4], IN[5], ~IN[6]);  // And
  nand nand_2 (ALU_B_SOURCE[0], ~IN[2], ~IN[3], IN[4], IN[5], ~IN[6]);  // NAnd
  and and_17 (ALU_B_SOURCE[1], ~IN[2], ~IN[3], IN[4], IN[5], ~IN[6]);  // And
  and and_18 (and_18_out, ~IN[2], ~IN[3], IN[4], ~IN[6], ~IN[12], IN[13], ~IN[14]);  // And
  and and_19 (and_19_out, ~IN[2], ~IN[3], IN[4], ~IN[6], IN[12], IN[13], ~IN[14]);  // And
  nand nand_3 (nand_3_out, ~IN[2], ~IN[3], IN[4], ~IN[6]);  // NAnd
  and and_20 (and_20_out, ~IN[2], ~IN[3], IN[4], IN[5], ~IN[6], ~IN[12], ~IN[13], ~IN[14], ~IN[30]);  // And
  and and_21 (and_21_out, ~IN[2], ~IN[3], IN[4], ~IN[5], ~IN[6], ~IN[12], ~IN[13], ~IN[14]);  // And
  and and_22 (ALU_INSTR[1], ~IN[2], ~IN[3], IN[4], ~IN[6], ~IN[12], IN[13], IN[14]);  // And
  and and_23 (ALU_INSTR[2], ~IN[2], ~IN[3], IN[4], ~IN[6], IN[12], IN[13], IN[14]);  // And
  and and_24 (ALU_INSTR[3], ~IN[2], ~IN[3], IN[4], ~IN[6], IN[12], ~IN[13], IN[14], ~IN[30]);  // And
  and and_25 (ALU_INSTR[4], ~IN[2], ~IN[3], IN[4], IN[5], ~IN[6], ~IN[12], ~IN[13], ~IN[14], IN[30]);  // And
  and and_26 (ALU_INSTR[5], ~IN[2], ~IN[3], IN[4], ~IN[6], ~IN[12], ~IN[13], IN[14]);  // And
  and and_27 (ALU_INSTR[6], ~IN[2], ~IN[3], IN[4], ~IN[6], IN[12], ~IN[13], ~IN[14]);  // And
  and and_28 (ALU_INSTR[7], ~IN[2], ~IN[3], IN[4], ~IN[6], IN[12], ~IN[13], IN[14], IN[30]);  // And
  and and_29 (COMP_SEL[0], ~IN[12], ~IN[13], ~IN[14]);  // And
  and and_30 (COMP_SEL[1], IN[12], ~IN[13], ~IN[14]);  // And
  and and_31 (COMP_SEL[2], ~IN[12], IN[13], ~IN[14]);  // And
  and and_32 (COMP_SEL[3], IN[12], IN[13], ~IN[14]);  // And
  and and_33 (COMP_SEL[4], ~IN[12], ~IN[13], IN[14]);  // And
  and and_34 (COMP_SEL[5], IN[12], ~IN[13], IN[14]);  // And
  and and_35 (COMP_SEL[6], ~IN[12], IN[13], IN[14]);  // And
  and and_36 (COMP_SEL[7], IN[12], IN[13], IN[14]);
  and and_37 (RESULT_IS_COMP, ~IN[2], ~IN[3], IN[4], ~IN[6], IN[13], ~IN[14]);  // And
  and and_38 (EXECUTE_RESULT_DESTINATION[0], ~IN[3], IN[4], ~IN[6]);  // And
  and and_39 (EXECUTE_RESULT_DESTINATION[1], IN[2], ~IN[4], IN[5], IN[6]);  // And
  and and_40 (EXECUTE_RESULT_DESTINATION[2], ~IN[2], ~IN[3], ~IN[4], IN[5], IN[6]);  // And
  and and_41 (EXECUTE_RESULT_DESTINATION[3], ~IN[2], ~IN[3], ~IN[4], ~IN[6]);  // And
  and and_42 (MEMORY_ACCESS[0], ~IN[2], ~IN[3], ~IN[4], ~IN[5], ~IN[6]);  // And
  and and_43 (MEMORY_ACCESS[4], ~IN[2], ~IN[3], ~IN[4], IN[5], ~IN[6]);  // And
  and and_44 (and_44_out, IN[0], IN[1], ~IN[2], ~IN[3], IN[4], IN[5], ~IN[6], ~IN[12], ~IN[13], ~IN[14], ~IN[25], ~IN[26], ~IN[27], ~IN[28], ~IN[29], ~IN[30], ~IN[31]);  // And
  and and_45 (and_45_out, IN[0], IN[1], ~IN[2], ~IN[3], IN[4], IN[5], ~IN[6], ~IN[12], ~IN[13], ~IN[14], ~IN[25], ~IN[26], ~IN[27], ~IN[28], ~IN[29], IN[30], ~IN[31]);  // And
  and and_46 (and_46_out, IN[0], IN[1], ~IN[2], ~IN[3], IN[4], IN[5], ~IN[6], IN[12], IN[13], IN[14], ~IN[25], ~IN[26], ~IN[27], ~IN[28], ~IN[29], ~IN[30], ~IN[31]);  // And
  and and_47 (and_47_out, IN[0], IN[1], ~IN[2], ~IN[3], IN[4], IN[5], ~IN[6], ~IN[12], IN[13], IN[14], ~IN[25], ~IN[26], ~IN[27], ~IN[28], ~IN[29], ~IN[30], ~IN[31]);  // And
  and and_48 (and_48_out, IN[0], IN[1], ~IN[2], ~IN[3], IN[4], IN[5], ~IN[6], ~IN[12], ~IN[13], IN[14], ~IN[25], ~IN[26], ~IN[27], ~IN[28], ~IN[29], ~IN[30], ~IN[31]);  // And
  and and_49 (and_49_out, IN[0], IN[1], ~IN[2], ~IN[3], IN[4], ~IN[5], ~IN[6], ~IN[12], ~IN[13], ~IN[14]);  // And
  and and_50 (and_50_out, IN[0], IN[1], ~IN[2], ~IN[3], IN[4], ~IN[5], ~IN[6], IN[12], IN[13], IN[14]);  // And
  and and_51 (and_51_out, IN[0], IN[1], ~IN[2], ~IN[3], IN[4], ~IN[5], ~IN[6], ~IN[12], IN[13], IN[14]);  // And
  and and_52 (and_52_out, IN[0], IN[1], ~IN[2], ~IN[3], IN[4], ~IN[5], ~IN[6], ~IN[12], ~IN[13], IN[14]);  // And
  and and_53 (and_53_out, IN[0], IN[1], ~IN[2], ~IN[3], IN[4], IN[5], ~IN[6], ~IN[12], ~IN[13], ~IN[14], ~IN[25], ~IN[26], ~IN[27], ~IN[28], IN[29], ~IN[30], ~IN[31]);  // And
  and and_54 (and_54_out, IN[0], IN[1], ~IN[2], ~IN[3], IN[4], IN[5], ~IN[6], IN[12], ~IN[13], IN[14], ~IN[25], ~IN[26], ~IN[27], ~IN[28], ~IN[29], ~IN[30], ~IN[31]);  // And
  and and_55 (and_55_out, IN[0], IN[1], ~IN[2], ~IN[3], IN[4], IN[5], ~IN[6], IN[12], ~IN[13], IN[14], ~IN[25], ~IN[26], ~IN[27], ~IN[28], ~IN[29], IN[30], ~IN[31]);  // And
  and and_56 (and_56_out, IN[0], IN[1], ~IN[2], ~IN[3], IN[4], ~IN[5], ~IN[6], IN[12], ~IN[13], ~IN[14], ~IN[25], ~IN[26], ~IN[27], ~IN[28], ~IN[29], ~IN[30], ~IN[31]);  // And
  and and_57 (and_57_out, IN[0], IN[1], ~IN[2], ~IN[3], IN[4], ~IN[5], ~IN[6], IN[12], ~IN[13], IN[14], ~IN[25], ~IN[26], ~IN[27], ~IN[28], ~IN[29], ~IN[30], ~IN[31]);  // And
  and and_58 (and_58_out, IN[0], IN[1], ~IN[2], ~IN[3], IN[4], ~IN[5], ~IN[6], IN[12], ~IN[13], IN[14], ~IN[25], ~IN[26], ~IN[27], ~IN[28], ~IN[29], IN[30], ~IN[31]);  // And
  and and_59 (and_59_out, IN[0], IN[1], ~IN[2], ~IN[3], IN[4], IN[5], ~IN[6], ~IN[12], IN[13], ~IN[14], ~IN[25], ~IN[26], ~IN[27], ~IN[28], ~IN[29], ~IN[30], ~IN[31]);  // And
  and and_60 (and_60_out, IN[0], IN[1], ~IN[2], ~IN[3], IN[4], IN[5], ~IN[6], IN[12], IN[13], ~IN[14], ~IN[25], ~IN[26], ~IN[27], ~IN[28], ~IN[29], ~IN[30], ~IN[31]);  // And
  and and_61 (and_61_out, IN[0], IN[1], ~IN[2], ~IN[3], IN[4], ~IN[5], ~IN[6], ~IN[12], IN[13], ~IN[14]);  // And
  and and_62 (and_62_out, IN[0], IN[1], ~IN[2], ~IN[3], IN[4], ~IN[5], ~IN[6], IN[12], IN[13], ~IN[14]);  // And
  and and_63 (and_63_out, IN[0], IN[1], IN[2], ~IN[3], IN[4], IN[5], ~IN[6]);  // And
  and and_64 (and_64_out, IN[0], IN[1], IN[2], ~IN[3], IN[4], ~IN[5], ~IN[6]);  // And
  and and_65 (and_65_out, IN[0], IN[1], IN[2], IN[3], ~IN[4], IN[5], IN[6]);  // And
  and and_66 (and_66_out, IN[0], IN[1], IN[2], ~IN[3], ~IN[4], IN[5], IN[6], ~IN[12], ~IN[13], ~IN[14]);  // And
  and and_67 (and_67_out, IN[0], IN[1], ~IN[2], ~IN[3], ~IN[4], IN[5], IN[6], ~IN[12], ~IN[13], ~IN[14]);  // And
  and and_68 (and_68_out, IN[0], IN[1], ~IN[2], ~IN[3], ~IN[4], IN[5], IN[6], IN[12], ~IN[13], ~IN[14]);  // And
  and and_69 (and_69_out, IN[0], IN[1], ~IN[2], ~IN[3], ~IN[4], IN[5], IN[6], ~IN[12], ~IN[13], IN[14]);  // And
  and and_70 (and_70_out, IN[0], IN[1], ~IN[2], ~IN[3], ~IN[4], IN[5], IN[6], IN[12], ~IN[13], IN[14]);  // And
  and and_71 (and_71_out, IN[0], IN[1], ~IN[2], ~IN[3], ~IN[4], IN[5], IN[6], ~IN[12], IN[13], IN[14]);  // And
  and and_72 (and_72_out, IN[0], IN[1], ~IN[2], ~IN[3], ~IN[4], IN[5], IN[6], IN[12], IN[13], IN[14]);  // And
  and and_73 (and_73_out, IN[0], IN[1], ~IN[2], ~IN[3], ~IN[4], ~IN[5], ~IN[6], ~IN[12], ~IN[13], ~IN[14]);  // And
  and and_74 (and_74_out, IN[0], IN[1], ~IN[2], ~IN[3], ~IN[4], ~IN[5], ~IN[6], IN[12], ~IN[13], ~IN[14]);  // And
  and and_75 (and_75_out, IN[0], IN[1], ~IN[2], ~IN[3], ~IN[4], ~IN[5], ~IN[6], ~IN[12], IN[13], ~IN[14]);  // And
  and and_76 (and_76_out, IN[0], IN[1], ~IN[2], ~IN[3], ~IN[4], ~IN[5], ~IN[6], ~IN[12], ~IN[13], IN[14]);  // And
  and and_77 (and_77_out, IN[0], IN[1], ~IN[2], ~IN[3], ~IN[4], ~IN[5], ~IN[6], IN[12], ~IN[13], IN[14]);  // And
  and and_78 (and_78_out, IN[0], IN[1], ~IN[2], ~IN[3], ~IN[4], IN[5], ~IN[6], ~IN[12], ~IN[13], ~IN[14]);  // And
  and and_79 (and_79_out, IN[0], IN[1], ~IN[2], ~IN[3], ~IN[4], IN[5], ~IN[6], IN[12], ~IN[13], ~IN[14]);  // And
  and and_80 (and_80_out, IN[0], IN[1], ~IN[2], ~IN[3], ~IN[4], IN[5], ~IN[6], ~IN[12], IN[13], ~IN[14]);  // And
  or or_1 (FORMAT[1], and_3_out, and_4_out, and_5_out);
  or or_2 (FORMAT[4], and_8_out, and_9_out);
  or or_3 (ALU_A_SOURCE[0], and_11_out, and_12_out);
  or or_4 (ALU_A_SOURCE[1], and_13_out, and_14_out, and_15_out);
  or or_5 (ALU_INSTR[0], and_18_out, and_19_out, nand_3_out, and_20_out, and_21_out);
  nor nor_1 (E, and_44_out, and_45_out, and_46_out, and_47_out, and_48_out, and_49_out, and_50_out, and_51_out, and_52_out, and_53_out, and_54_out, and_55_out, and_56_out, and_57_out, and_58_out, and_59_out, and_60_out, and_61_out, and_62_out, and_63_out, and_64_out, and_65_out, and_66_out, and_67_out, and_68_out, and_69_out, and_70_out, and_71_out, and_72_out, and_73_out, and_74_out, and_75_out, and_76_out, and_77_out, and_78_out, and_79_out, and_80_out);
  // Pins of 1 and 8 bits meet at MEMORY_ACCESS
  // Pins of 1 and 4 bits meet at MEMORY_ACCESS[3:0]
  // Pins of 1 and 4 bits meet at MEMORY_ACCESS[7:4]

  // Notes on the sheet:
  //   IN: default 20191123
  //   Control Transfer
  //   Write to Register
  //   SLT
  //   SLTU
  //   OTHER
  //   ADD
  //   ADDI
  //   OR
  //   AND
  //   SRL
  //   SUB
  //   XOR
  //   SLL
  //   SRA
  //   ANDI
  //   ORI
  //   XORI
  //   SLLI
  //   SRLI
  //   SRAI
  //   SLTI
  //   SLTIU
  //   LUI
  //   AUIPC
  //   JAL
  //   JALR
  //   BEQ
  //   BNE
  //   BLT
  //   BGE
  //   BLTU
  //   BGEU
  //   LB
  //   LH
  //   LW
  //   LBU
  //   LHU
  //   SB
  //   SH
  //   SW
endmodule
