// Digital circuit RV32I-Instruction-Display.dig as structural Verilog
module RV32I_Instruction_Display (
  input  [31:0] INSTR
);

  wire and_1_out, and_2_out, and_3_out, and_4_out, and_5_out, and_6_out, and_7_out, and_8_out, and_9_out,
       and_10_out, and_11_out, and_12_out, and_13_out, and_14_out, and_15_out, and_16_out, and_17_out,
       and_18_out, and_19_out, and_20_out, and_21_out, and_22_out, and_23_out, and_24_out, and_25_out,
       and_26_out, and_27_out, and_28_out, and_29_out, and_30_out, and_31_out, and_32_out, and_33_out,
       and_34_out, and_35_out, and_36_out, and_37_out, nor_1_out;
  wire [15:0] driver_1_out, driver_2_out, driver_3_out, driver_15_out, driver_62_out, pulldown_27_out,
       pulldown_28_out, pulldown_29_out;

  and and_1 (and_1_out, INSTR[0], INSTR[1], ~INSTR[2], ~INSTR[3], INSTR[4], INSTR[5], ~INSTR[6], ~INSTR[12], ~INSTR[13], ~INSTR[14], ~INSTR[25], ~INSTR[26], ~INSTR[27], ~INSTR[28], ~INSTR[29], ~INSTR[30], ~INSTR[31]);  // And
  and and_2 (and_2_out, INSTR[0], INSTR[1], ~INSTR[2], ~INSTR[3], INSTR[4], INSTR[5], ~INSTR[6], ~INSTR[12], ~INSTR[13], ~INSTR[14], ~INSTR[25], ~INSTR[26], ~INSTR[27], ~INSTR[28], ~INSTR[29], INSTR[30], ~INSTR[31]);  // And
  and and_3 (and_3_out, INSTR[0], INSTR[1], ~INSTR[2], ~INSTR[3], INSTR[4], INSTR[5], ~INSTR[6], INSTR[12], INSTR[13], INSTR[14], ~INSTR[25], ~INSTR[26], ~INSTR[27], ~INSTR[28], ~INSTR[29], ~INSTR[30], ~INSTR[31]);  // And
  and and_4 (and_4_out, INSTR[0], INSTR[1], ~INSTR[2], ~INSTR[3], INSTR[4], INSTR[5], ~INSTR[6], ~INSTR[12], INSTR[13], INSTR[14], ~INSTR[25], ~INSTR[26], ~INSTR[27], ~INSTR[28], ~INSTR[29], ~INSTR[30], ~INSTR[31]);  // And
  and and_5 (and_5_out, INSTR[0], INSTR[1], ~INSTR[2], ~INSTR[3], INSTR[4], INSTR[5], ~INSTR[6], ~INSTR[12], ~INSTR[13], INSTR[14], ~INSTR[25], ~INSTR[26], ~INSTR[27], ~INSTR[28], ~INSTR[29], ~INSTR[30], ~INSTR[31]);  // And
  and and_6 (and_6_out, INSTR[0], INSTR[1], ~INSTR[2], ~INSTR[3], INSTR[4], ~INSTR[5], ~INSTR[6], ~INSTR[12], ~INSTR[13], ~INSTR[14], ~INSTR[25], ~INSTR[26], ~INSTR[27], ~INSTR[28], ~INSTR[29], ~INSTR[30], ~INSTR[31]);  // And
  and and_7 (and_7_out, INSTR[0], INSTR[1], ~INSTR[2], ~INSTR[3], INSTR[4], ~INSTR[5], ~INSTR[6], INSTR[12], INSTR[13], INSTR[14], ~INSTR[25], ~INSTR[26], ~INSTR[27], ~INSTR[28], ~INSTR[29], ~INSTR[30], ~INSTR[31]);  // And
  and and_8 (and_8_out, INSTR[0], INSTR[1], ~INSTR[2], ~INSTR[3], INSTR[4], ~INSTR[5], ~INSTR[6], ~INSTR[12], INSTR[13], INSTR[14], ~INSTR[25], ~INSTR[26], ~INSTR[27], ~INSTR[28], ~INSTR[29], ~INSTR[30], ~INSTR[31]);  // And
  and and_9 (and_9_out, INSTR[0], INSTR[1], ~INSTR[2], ~INSTR[3], INSTR[4], ~INSTR[5], ~INSTR[6], ~INSTR[12], ~INSTR[13], INSTR[14], ~INSTR[25], ~INSTR[26], ~INSTR[27], ~INSTR[28], ~INSTR[29], ~INSTR[30], ~INSTR[31]);  // And
  and and_10 (and_10_out, INSTR[0], INSTR[1], ~INSTR[2], ~INSTR[3], INSTR[4], INSTR[5], ~INSTR[6], INSTR[12], ~INSTR[13], ~INSTR[14], ~INSTR[25], ~INSTR[26], ~INSTR[27], ~INSTR[28], ~INSTR[29], ~INSTR[30], ~INSTR[31]);  // And
  and and_11 (and_11_out, INSTR[0], INSTR[1], ~INSTR[2], ~INSTR[3], INSTR[4], INSTR[5], ~INSTR[6], INSTR[12], ~INSTR[13], INSTR[14], ~INSTR[25], ~INSTR[26], ~INSTR[27], ~INSTR[28], ~INSTR[29], ~INSTR[30], ~INSTR[31]);  // And
  and and_12 (and_12_out, INSTR[0], INSTR[1], ~INSTR[2], ~INSTR[3], INSTR[4], INSTR[5], ~INSTR[6], INSTR[12], ~INSTR[13], INSTR[14], ~INSTR[25], ~INSTR[26], ~INSTR[27], ~INSTR[28], ~INSTR[29], INSTR[30], ~INSTR[31]);  // And
  and and_13 (and_13_out, INSTR[0], INSTR[1], ~INSTR[2], ~INSTR[3], INSTR[4], ~INSTR[5], ~INSTR[6], INSTR[12], ~INSTR[13], ~INSTR[14], ~INSTR[25], ~INSTR[26], ~INSTR[27], ~INSTR[28], ~INSTR[29], ~INSTR[30], ~INSTR[31]);  // And
  and and_14 (and_14_out, INSTR[0], INSTR[1], ~INSTR[2], ~INSTR[3], INSTR[4], ~INSTR[5], ~INSTR[6], INSTR[12], ~INSTR[13], INSTR[14], ~INSTR[25], ~INSTR[26], ~INSTR[27], ~INSTR[28], ~INSTR[29], ~INSTR[30], ~INSTR[31]);  // And
  and and_15 (and_15_out, INSTR[0], INSTR[1], ~INSTR[2], ~INSTR[3], INSTR[4], ~INSTR[5], ~INSTR[6], INSTR[12], ~INSTR[13], INSTR[14], ~INSTR[25], ~INSTR[26], ~INSTR[27], ~INSTR[28], ~INSTR[29], INSTR[30], ~INSTR[31]);  // And
  and and_16 (and_16_out, INSTR[0], INSTR[1], ~INSTR[2], ~INSTR[3], INSTR[4], INSTR[5], ~INSTR[6], ~INSTR[12], INSTR[13], ~INSTR[14], ~INSTR[25], ~INSTR[26], ~INSTR[27], ~INSTR[28], ~INSTR[29], ~INSTR[30], ~INSTR[31]);  // And
  and and_17 (and_17_out, INSTR[0], INSTR[1], ~INSTR[2], ~INSTR[3], INSTR[4], INSTR[5], ~INSTR[6], INSTR[12], INSTR[13], ~INSTR[14], ~INSTR[25], ~INSTR[26], ~INSTR[27], ~INSTR[28], ~INSTR[29], ~INSTR[30], ~INSTR[31]);  // And
  and and_18 (and_18_out, INSTR[0], INSTR[1], ~INSTR[2], ~INSTR[3], INSTR[4], ~INSTR[5], ~INSTR[6], ~INSTR[12], INSTR[13], ~INSTR[14], ~INSTR[25], ~INSTR[26], ~INSTR[27], ~INSTR[28], ~INSTR[29], ~INSTR[30], ~INSTR[31]);  // And
  and and_19 (and_19_out, INSTR[0], INSTR[1], ~INSTR[2], ~INSTR[3], INSTR[4], ~INSTR[5], ~INSTR[6], INSTR[12], INSTR[13], ~INSTR[14], ~INSTR[25], ~INSTR[26], ~INSTR[27], ~INSTR[28], ~INSTR[29], ~INSTR[30], ~INSTR[31]);  // And
  and and_20 (and_20_out, INSTR[0], INSTR[1], INSTR[2], ~INSTR[3], INSTR[4], INSTR[5], ~INSTR[6]);  // And
  and and_21 (and_21_out, INSTR[0], INSTR[1], INSTR[2], ~INSTR[3], INSTR[4], ~INSTR[5], ~INSTR[6]);  // And
  and and_22 (and_22_out, INSTR[0], INSTR[1], INSTR[2], INSTR[3], ~INSTR[4], INSTR[5], INSTR[6]);  // And
  and and_23 (and_23_out, INSTR[0], INSTR[1], INSTR[2], ~INSTR[3], ~INSTR[4], INSTR[5], INSTR[6], ~INSTR[12], ~INSTR[13], ~INSTR[14]);  // And
  and and_24 (and_24_out, INSTR[0], INSTR[1], ~INSTR[2], ~INSTR[3], ~INSTR[4], INSTR[5], INSTR[6], ~INSTR[12], ~INSTR[13], ~INSTR[14]);  // And
  and and_25 (and_25_out, INSTR[0], INSTR[1], ~INSTR[2], ~INSTR[3], ~INSTR[4], INSTR[5], INSTR[6], INSTR[12], ~INSTR[13], ~INSTR[14]);  // And
  and and_26 (and_26_out, INSTR[0], INSTR[1], ~INSTR[2], ~INSTR[3], ~INSTR[4], INSTR[5], INSTR[6], ~INSTR[12], ~INSTR[13], INSTR[14]);  // And
  and and_27 (and_27_out, INSTR[0], INSTR[1], ~INSTR[2], ~INSTR[3], ~INSTR[4], INSTR[5], INSTR[6], INSTR[12], ~INSTR[13], INSTR[14]);  // And
  and and_28 (and_28_out, INSTR[0], INSTR[1], ~INSTR[2], ~INSTR[3], ~INSTR[4], INSTR[5], INSTR[6], ~INSTR[12], INSTR[13], INSTR[14]);  // And
  and and_29 (and_29_out, INSTR[0], INSTR[1], ~INSTR[2], ~INSTR[3], ~INSTR[4], INSTR[5], INSTR[6], INSTR[12], INSTR[13], INSTR[14]);  // And
  and and_30 (and_30_out, INSTR[0], INSTR[1], ~INSTR[2], ~INSTR[3], ~INSTR[4], ~INSTR[5], ~INSTR[6], ~INSTR[12], ~INSTR[13], ~INSTR[14]);  // And
  and and_31 (and_31_out, INSTR[0], INSTR[1], ~INSTR[2], ~INSTR[3], ~INSTR[4], ~INSTR[5], ~INSTR[6], INSTR[12], ~INSTR[13], ~INSTR[14]);  // And
  and and_32 (and_32_out, INSTR[0], INSTR[1], ~INSTR[2], ~INSTR[3], ~INSTR[4], ~INSTR[5], ~INSTR[6], ~INSTR[12], INSTR[13], ~INSTR[14]);  // And
  and and_33 (and_33_out, INSTR[0], INSTR[1], ~INSTR[2], ~INSTR[3], ~INSTR[4], ~INSTR[5], ~INSTR[6], ~INSTR[12], ~INSTR[13], INSTR[14]);  // And
  and and_34 (and_34_out, INSTR[0], INSTR[1], ~INSTR[2], ~INSTR[3], ~INSTR[4], ~INSTR[5], ~INSTR[6], INSTR[12], ~INSTR[13], INSTR[14]);  // And
  and and_35 (and_35_out, INSTR[0], INSTR[1], ~INSTR[2], ~INSTR[3], ~INSTR[4], INSTR[5], ~INSTR[6], ~INSTR[12], ~INSTR[13], ~INSTR[14]);  // And
  and and_36 (and_36_out, INSTR[0], INSTR[1], ~INSTR[2], ~INSTR[3], ~INSTR[4], INSTR[5], ~INSTR[6], INSTR[12], ~INSTR[13], ~INSTR[14]);  // And
  and and_37 (and_37_out, INSTR[0], INSTR[1], ~INSTR[2], ~INSTR[3], ~INSTR[4], INSTR[5], ~INSTR[6], ~INSTR[12], INSTR[13], ~INSTR[14]);  // And
  nor nor_1 (nor_1_out, and_1_out, and_2_out, and_3_out, and_4_out, and_5_out, and_6_out, and_7_out, and_8_out, and_9_out, and_10_out, and_11_out, and_12_out, and_13_out, and_14_out, and_15_out, and_16_out, and_17_out, and_18_out, and_19_out, and_20_out, and_21_out, and_22_out, and_23_out, and_24_out, and_25_out, and_26_out, and_27_out, and_28_out, and_29_out, and_30_out, and_31_out, and_32_out, and_33_out, and_34_out, and_35_out, and_36_out, and_37_out);
  PullDown #(.Bits(16)) pulldown_1 (.out(16'h3cf));
  PullDown #(.Bits(16)) pulldown_2 (.out(16'h4a3f));
  PullDown #(.Bits(16)) pulldown_3 (.out(16'hf3));
  PullDown #(.Bits(16)) pulldown_4 (.out(16'h483f));
  PullDown #(.Bits(16)) pulldown_5 (.out(16'h3f3));
  PullDown #(.Bits(16)) pulldown_6 (.out(16'h3c3));
  PullDown #(.Bits(16)) pulldown_7 (.out(16'h2fb));
  PullDown #(.Bits(16)) pulldown_8 (.out(16'h3cc));
  PullDown #(.Bits(16)) pulldown_9 (.out(16'h4833));
  PullDown #(.Bits(16)) pulldown_10 (.out(16'h7c));
  PullDown #(.Bits(16)) pulldown_11 (.out(16'h31c0));
  PullDown #(.Bits(16)) pulldown_12 (.out(16'hf0));
  PullDown #(.Bits(16)) pulldown_13 (.out(16'h14cc));
  PullDown #(.Bits(16)) pulldown_14 (.out(16'h24cc));
  PullDown #(.Bits(16)) pulldown_15 (.out(16'hff));
  PullDown #(.Bits(16)) pulldown_16 (.out(16'h3c7));
  PullDown #(.Bits(16)) pulldown_17 (.out(16'h20ff));
  PullDown #(.Bits(16)) pulldown_18 (.out(16'h23c7));
  PullDown #(.Bits(16)) pulldown_19 (.out(16'h63b));
  PullDown #(.Bits(16)) pulldown_20 (.out(16'h4803));
  PullDown #(.Bits(16)) pulldown_21 (.out(16'hfc));
  PullDown #(.Bits(16)) pulldown_22 (.out(16'h90c0));
  PullDown #(.Bits(16)) pulldown_23 (.out(16'ha0cc));
  PullDown #(.Bits(16)) pulldown_24 (.out(16'hb400));
  PullDown #(.Bits(16)) pulldown_25 (.out(16'h5400));
  assign driver_1_out = and_1_out ? 16'h3cf : 16'bz;  // Driver driver_1
  assign driver_2_out = and_1_out ? 16'h483f : 16'bz;  // Driver driver_2
  assign driver_3_out = and_1_out ? 16'h483f : 16'bz;  // Driver driver_3
  assign driver_1_out = and_2_out ? 16'h63b : 16'bz;  // Driver driver_4
  assign driver_2_out = and_2_out ? 16'hfc : 16'bz;  // Driver driver_5
  assign driver_3_out = and_2_out ? 16'h4a3f : 16'bz;  // Driver driver_6
  assign driver_1_out = and_3_out ? 16'h3cf : 16'bz;  // Driver driver_7
  assign driver_2_out = and_3_out ? 16'h24cc : 16'bz;  // Driver driver_8
  assign driver_3_out = and_3_out ? 16'h483f : 16'bz;  // Driver driver_9
  assign driver_2_out = and_4_out ? 16'hff : 16'bz;  // Driver driver_10
  assign driver_3_out = and_4_out ? 16'h23c7 : 16'bz;  // Driver driver_11
  assign driver_1_out = and_5_out ? 16'hb400 : 16'bz;  // Driver driver_12
  assign driver_2_out = and_5_out ? 16'hff : 16'bz;  // Driver driver_13
  assign driver_3_out = and_5_out ? 16'h23c7 : 16'bz;  // Driver driver_14
  assign driver_15_out = and_6_out ? 16'h3cf : 16'bz;  // Driver driver_15
  assign driver_1_out = and_6_out ? 16'h483f : 16'bz;  // Driver driver_16
  assign driver_2_out = and_6_out ? 16'h483f : 16'bz;  // Driver driver_17
  assign driver_3_out = and_6_out ? 16'h4833 : 16'bz;  // Driver driver_18
  assign driver_15_out = and_7_out ? 16'h3cf : 16'bz;  // Driver driver_19
  assign driver_1_out = and_7_out ? 16'h24cc : 16'bz;  // Driver driver_20
  assign driver_2_out = and_7_out ? 16'h483f : 16'bz;  // Driver driver_21
  assign driver_3_out = and_7_out ? 16'h4833 : 16'bz;  // Driver driver_22
  assign driver_1_out = and_8_out ? 16'hff : 16'bz;  // Driver driver_23
  assign driver_2_out = and_8_out ? 16'h23c7 : 16'bz;  // Driver driver_24
  assign driver_3_out = and_8_out ? 16'h4833 : 16'bz;  // Driver driver_25
  assign driver_15_out = and_9_out ? 16'hb400 : 16'bz;  // Driver driver_26
  assign driver_1_out = and_9_out ? 16'hff : 16'bz;  // Driver driver_27
  assign driver_2_out = and_9_out ? 16'h23c7 : 16'bz;  // Driver driver_28
  assign driver_3_out = and_9_out ? 16'h4833 : 16'bz;  // Driver driver_29
  assign driver_1_out = and_10_out ? 16'h63b : 16'bz;  // Driver driver_30
  assign driver_2_out = and_10_out ? 16'hf0 : 16'bz;  // Driver driver_31
  assign driver_3_out = and_10_out ? 16'hf0 : 16'bz;  // Driver driver_32
  assign driver_1_out = and_11_out ? 16'h63b : 16'bz;  // Driver driver_33
  assign driver_2_out = and_11_out ? 16'h23c7 : 16'bz;  // Driver driver_34
  assign driver_3_out = and_11_out ? 16'hf0 : 16'bz;  // Driver driver_35
  assign driver_1_out = and_12_out ? 16'h63b : 16'bz;  // Driver driver_36
  assign driver_2_out = and_12_out ? 16'h23c7 : 16'bz;  // Driver driver_37
  assign driver_3_out = and_12_out ? 16'h3cf : 16'bz;  // Driver driver_38
  assign driver_15_out = and_13_out ? 16'h63b : 16'bz;  // Driver driver_39
  assign driver_1_out = and_13_out ? 16'hf0 : 16'bz;  // Driver driver_40
  assign driver_2_out = and_13_out ? 16'hf0 : 16'bz;  // Driver driver_41
  assign driver_3_out = and_13_out ? 16'h4833 : 16'bz;  // Driver driver_42
  assign driver_15_out = and_14_out ? 16'h63b : 16'bz;  // Driver driver_43
  assign driver_1_out = and_14_out ? 16'h23c7 : 16'bz;  // Driver driver_44
  assign driver_2_out = and_14_out ? 16'hf0 : 16'bz;  // Driver driver_45
  assign driver_3_out = and_14_out ? 16'h4833 : 16'bz;  // Driver driver_46
  assign driver_15_out = and_15_out ? 16'h63b : 16'bz;  // Driver driver_47
  assign driver_1_out = and_15_out ? 16'h23c7 : 16'bz;  // Driver driver_48
  assign driver_2_out = and_15_out ? 16'h3cf : 16'bz;  // Driver driver_49
  assign driver_3_out = and_15_out ? 16'h4833 : 16'bz;  // Driver driver_50
  assign driver_1_out = and_16_out ? 16'h63b : 16'bz;  // Driver driver_51
  assign driver_2_out = and_16_out ? 16'hf0 : 16'bz;  // Driver driver_52
  assign driver_3_out = and_16_out ? 16'h4803 : 16'bz;  // Driver driver_53
  assign driver_15_out = and_17_out ? 16'h63b : 16'bz;  // Driver driver_54
  assign driver_1_out = and_17_out ? 16'hf0 : 16'bz;  // Driver driver_55
  assign driver_2_out = and_17_out ? 16'h4803 : 16'bz;  // Driver driver_56
  assign driver_3_out = and_17_out ? 16'hfc : 16'bz;  // Driver driver_57
  assign driver_15_out = and_18_out ? 16'h63b : 16'bz;  // Driver driver_58
  assign driver_1_out = and_18_out ? 16'hf0 : 16'bz;  // Driver driver_59
  assign driver_2_out = and_18_out ? 16'h4803 : 16'bz;  // Driver driver_60
  assign driver_3_out = and_18_out ? 16'h4833 : 16'bz;  // Driver driver_61
  assign driver_62_out = and_19_out ? 16'h63b : 16'bz;  // Driver driver_62
  assign driver_15_out = and_19_out ? 16'hf0 : 16'bz;  // Driver driver_63
  assign driver_1_out = and_19_out ? 16'h4803 : 16'bz;  // Driver driver_64
  assign driver_2_out = and_19_out ? 16'h4833 : 16'bz;  // Driver driver_65
  assign driver_3_out = and_19_out ? 16'hfc : 16'bz;  // Driver driver_66
  assign driver_1_out = and_20_out ? 16'hf0 : 16'bz;  // Driver driver_67
  assign driver_2_out = and_20_out ? 16'hfc : 16'bz;  // Driver driver_68
  assign driver_3_out = and_20_out ? 16'h4833 : 16'bz;  // Driver driver_69
  assign driver_62_out = and_21_out ? 16'h3cf : 16'bz;  // Driver driver_70
  assign driver_15_out = and_21_out ? 16'hfc : 16'bz;  // Driver driver_71
  assign driver_1_out = and_21_out ? 16'h4833 : 16'bz;  // Driver driver_72
  assign driver_2_out = and_21_out ? 16'h3c7 : 16'bz;  // Driver driver_73
  assign driver_3_out = and_21_out ? 16'hf3 : 16'bz;  // Driver driver_74
  assign driver_1_out = and_22_out ? 16'h7c : 16'bz;  // Driver driver_75
  assign driver_2_out = and_22_out ? 16'h3cf : 16'bz;  // Driver driver_76
  assign driver_3_out = and_22_out ? 16'hf0 : 16'bz;  // Driver driver_77
  assign driver_15_out = and_23_out ? 16'h7c : 16'bz;  // Driver driver_78
  assign driver_1_out = and_23_out ? 16'h3cf : 16'bz;  // Driver driver_79
  assign driver_2_out = and_23_out ? 16'hf0 : 16'bz;  // Driver driver_80
  assign driver_3_out = and_23_out ? 16'h23c7 : 16'bz;  // Driver driver_81
  assign driver_1_out = and_24_out ? 16'h4a3f : 16'bz;  // Driver driver_82
  assign driver_2_out = and_24_out ? 16'h3f3 : 16'bz;  // Driver driver_83
  assign driver_3_out = and_24_out ? 16'h20ff : 16'bz;  // Driver driver_84
  assign driver_1_out = and_25_out ? 16'h4a3f : 16'bz;  // Driver driver_85
  assign driver_2_out = and_25_out ? 16'h24cc : 16'bz;  // Driver driver_86
  assign driver_3_out = and_25_out ? 16'h3f3 : 16'bz;  // Driver driver_87
  assign driver_1_out = and_26_out ? 16'h4a3f : 16'bz;  // Driver driver_88
  assign driver_2_out = and_26_out ? 16'hf0 : 16'bz;  // Driver driver_89
  assign driver_3_out = and_26_out ? 16'h4803 : 16'bz;  // Driver driver_90
  assign driver_1_out = and_27_out ? 16'h4a3f : 16'bz;  // Driver driver_91
  assign driver_2_out = and_27_out ? 16'h2fb : 16'bz;  // Driver driver_92
  assign driver_3_out = and_27_out ? 16'h3f3 : 16'bz;  // Driver driver_93
  assign driver_15_out = and_28_out ? 16'h4a3f : 16'bz;  // Driver driver_94
  assign driver_1_out = and_28_out ? 16'hf0 : 16'bz;  // Driver driver_95
  assign driver_2_out = and_28_out ? 16'h4803 : 16'bz;  // Driver driver_96
  assign driver_3_out = and_28_out ? 16'hfc : 16'bz;  // Driver driver_97
  assign driver_15_out = and_29_out ? 16'h4a3f : 16'bz;  // Driver driver_98
  assign driver_1_out = and_29_out ? 16'h2fb : 16'bz;  // Driver driver_99
  assign driver_2_out = and_29_out ? 16'h3f3 : 16'bz;  // Driver driver_100
  assign driver_3_out = and_29_out ? 16'hfc : 16'bz;  // Driver driver_101
  assign driver_2_out = and_30_out ? 16'hf0 : 16'bz;  // Driver driver_102
  assign driver_3_out = and_30_out ? 16'h4a3f : 16'bz;  // Driver driver_103
  assign driver_2_out = and_31_out ? 16'hf0 : 16'bz;  // Driver driver_104
  assign driver_3_out = and_31_out ? 16'h3cc : 16'bz;  // Driver driver_105
  assign driver_2_out = and_32_out ? 16'hf0 : 16'bz;  // Driver driver_106
  assign driver_3_out = and_32_out ? 16'ha0cc : 16'bz;  // Driver driver_107
  assign driver_1_out = and_33_out ? 16'hf0 : 16'bz;  // Driver driver_108
  assign driver_2_out = and_33_out ? 16'h4a3f : 16'bz;  // Driver driver_109
  assign driver_3_out = and_33_out ? 16'hfc : 16'bz;  // Driver driver_110
  assign driver_1_out = and_34_out ? 16'hf0 : 16'bz;  // Driver driver_111
  assign driver_2_out = and_34_out ? 16'h3cc : 16'bz;  // Driver driver_112
  assign driver_3_out = and_34_out ? 16'hfc : 16'bz;  // Driver driver_113
  assign driver_2_out = and_35_out ? 16'h63b : 16'bz;  // Driver driver_114
  assign driver_3_out = and_35_out ? 16'h4a3f : 16'bz;  // Driver driver_115
  assign driver_2_out = and_36_out ? 16'h63b : 16'bz;  // Driver driver_116
  assign driver_3_out = and_36_out ? 16'h3cc : 16'bz;  // Driver driver_117
  assign driver_2_out = and_37_out ? 16'h63b : 16'bz;  // Driver driver_118
  assign driver_3_out = and_37_out ? 16'ha0cc : 16'bz;  // Driver driver_119
  assign driver_62_out = nor_1_out ? 16'h3f3 : 16'bz;  // Driver driver_120
  assign driver_15_out = nor_1_out ? 16'h23c7 : 16'bz;  // Driver driver_121
  assign driver_1_out = nor_1_out ? 16'h23c7 : 16'bz;  // Driver driver_122
  assign driver_2_out = nor_1_out ? 16'hff : 16'bz;  // Driver driver_123
  assign driver_3_out = nor_1_out ? 16'h23c7 : 16'bz;  // Driver driver_124
  PullDown #(.Bits(16)) pulldown_26 (.out(16'h9033));
  PullDown #(.Bits(16)) pulldown_27 (.out(pulldown_27_out));
  PullDown #(.Bits(16)) pulldown_28 (.out(pulldown_28_out));
  PullDown #(.Bits(16)) pulldown_29 (.out(pulldown_29_out));
  PullDown #(.Bits(16)) pulldown_30 (.out(driver_62_out));
  PullDown #(.Bits(16)) pulldown_31 (.out(driver_15_out));
  PullDown #(.Bits(16)) pulldown_32 (.out(driver_1_out));
  PullDown #(.Bits(16)) pulldown_33 (.out(driver_2_out));
  PullDown #(.Bits(16)) pulldown_34 (.out(driver_3_out));
  SixteenSeg sixteenseg_1 (.led(pulldown_28_out), .dp(1'b0));
  SixteenSeg sixteenseg_2 (.led(pulldown_27_out), .dp(1'b0));
  SixteenSeg sixteenseg_3 (.led(pulldown_29_out), .dp(1'b0));
  SixteenSeg sixteenseg_4 (.led(driver_62_out), .dp(1'b0));
  SixteenSeg sixteenseg_5 (.led(driver_15_out), .dp(1'b0));
  SixteenSeg sixteenseg_6 (.led(driver_1_out), .dp(1'b0));
  SixteenSeg sixteenseg_7 (.led(driver_2_out), .dp(1'b0));
  SixteenSeg sixteenseg_8 (.led(driver_3_out), .dp(1'b0));

  // Notes on the sheet:
  //   INSTR: default 4099
  //   LUI
  //   JAL
  //   ADD
  //   SUB
  //   AND
  //   OR
  //   XOR
  //   ADDI
  //   ANDI
  //   ORI
  //   XORI
  //   SLL
  //   SRL
  //   SRA
  //   SLLI
  //   SRLI
  //   SRAI
  //   SLT
  //   SLTU
  //   SLTI
  //   SLTIU
  //   AUIPC
  //   JALR
  //   BEQ
  //   BNE
  //   BLT
  //   BGE
  //   BLTU
  //   BGEU
  //   LB
  //   LH
  //   LW
  //   LBU
  //   LHU
  //   SB
  //   SH
  //   SW
  //   A
  //   B
  //   C
  //   D
  //   E
  //   F
  //   G
  //   H
  //   I
  //   J
  //   K
  //   L
  //   M
  //   N
  //   O
  //   P
  //   Q
  //   R
  //   S
  //   T
  //   U
  //   V
  //   W
  //   X
  //   Y
  //   Z
endmodule
