// Digital circuit RV32I-Memory-Control.dig as structural Verilog
module RV32I_Memory_Control (
  input  [31:0] INSTR,
  input  Normal,
  input  Run,
  output MEMORY_HOLD,
  output MEMORY_EN,
  output ALU_SET_REGISTER,
  output COMP_SET_REGISTER,
  output MEMORY_SET_REGISTER,
  output WRITE_TO_MEMORY,
  output ACCESS_MEMORY
);

  wire rv32i_memory_instruction_decoder_1_memory_access, rv32i_memory_instruction_decoder_1_write_memory;

  RV32I_Memory_Instruction_Decoder rv32i_memory_instruction_decoder_1 (
    .IN(INSTR), .DATA_SOURCE({MEMORY_SET_REGISTER, COMP_SET_REGISTER, ALU_SET_REGISTER}),
    .WRITE_MEMORY(rv32i_memory_instruction_decoder_1_write_memory),
    .MEMORY_ACCESS(rv32i_memory_instruction_decoder_1_memory_access));
  and and_1 (MEMORY_HOLD, ~INSTR[4], INSTR[5], INSTR[6]);  // And
  and and_2 (MEMORY_EN, Normal, Run);
  and and_3 (WRITE_TO_MEMORY, rv32i_memory_instruction_decoder_1_write_memory, Normal);
  and and_4 (ACCESS_MEMORY, rv32i_memory_instruction_decoder_1_memory_access, Normal);
endmodule
