// Digital circuit RV32I-Memory-Instruction-Decoder.dig as structural Verilog
module RV32I_Memory_Instruction_Decoder (
  input  [31:0] IN,
  output [2:0] DATA_SOURCE,
  output WRITE_MEMORY,
  output MEMORY_ACCESS
);

  wire and_1_out, and_2_out, and_3_out, and_4_out;

  and and_1 (and_1_out, ~IN[2], ~IN[3], IN[4], ~IN[6], ~IN[13], ~IN[14]);  // And
  and and_2 (and_2_out, ~IN[2], ~IN[3], IN[4], ~IN[6], ~IN[13], IN[14]);  // And
  and and_3 (and_3_out, ~IN[2], ~IN[3], IN[4], ~IN[6], IN[13], IN[14]);  // And
  and and_4 (and_4_out, IN[2], ~IN[3], IN[4], ~IN[6]);  // And
  and and_5 (DATA_SOURCE[1], ~IN[2], ~IN[3], IN[4], ~IN[6], IN[13], ~IN[14]);  // And
  and and_6 (DATA_SOURCE[2], IN[0], IN[1], ~IN[2], ~IN[3], ~IN[4], ~IN[5], ~IN[6]);  // And
  and and_7 (WRITE_MEMORY, ~IN[2], ~IN[3], ~IN[4], IN[5], ~IN[6]);  // And
  and and_8 (MEMORY_ACCESS, ~IN[2], ~IN[3], ~IN[4], ~IN[6]);  // And
  or or_1 (DATA_SOURCE[0], and_1_out, and_2_out, and_3_out, and_4_out);

  // Notes on the sheet:
  //   IN: default 24849459
endmodule
