// Digital circuit RV32I-Register-Reserve.dig as structural Verilog
module RV32I_Register_Reserve (
  input  [31:0] INSTR,
  input  CLC,
  input  RD,
  input  RS1,
  input  RS2,
  output HOLD,
  output [4:0] E,
  output [4:0] O
);

  wire and_1_out, and_2_out, comparator_1_eq, comparator_2_eq, comparator_3_eq, comparator_4_eq, or_1_out,
       or_2_out, or_3_out, or_4_out, or_5_out, t_ff_1_nq, t_ff_1_q;
  wire [4:0] driver_1_out, driver_2_out, driver_3_out;

  or or_1 (or_1_out, RD, RS1, RS2);
  T_FF t_ff_1 (.T(or_1_out), .C(CLC), .Q(t_ff_1_q), .nQ(t_ff_1_nq));
  assign driver_1_out = RD ? INSTR[11:7] : 5'bz;  // Driver driver_1
  Register #(.Bits(5)) REGISTER_RESERVE_EVEN (.D(driver_1_out), .C(CLC), .en(t_ff_1_q), .Q(E));
  Register #(.Bits(5)) REGISTER_RESERVE_ODD (.D(driver_1_out), .C(CLC), .en(t_ff_1_nq), .Q(O));
  PullDown #(.Bits(5)) pulldown_1 (.out(driver_1_out));
  assign driver_2_out = RS1 ? INSTR[19:15] : 5'bz;  // Driver driver_2
  assign driver_3_out = RS2 ? INSTR[24:20] : 5'bz;  // Driver driver_3
  PullDown #(.Bits(5)) pulldown_2 (.out(driver_2_out));
  PullDown #(.Bits(5)) pulldown_3 (.out(driver_3_out));
  Comparator #(.Bits(5)) comparator_1 (.a(E), .b(driver_2_out), .eq(comparator_1_eq));  // open: gt, lt
  Comparator #(.Bits(5)) comparator_2 (.a(O), .b(driver_2_out), .eq(comparator_2_eq));  // open: gt, lt
  or or_2 (or_2_out, E[0], E[1], E[2], E[3], E[4]);
  or or_3 (or_3_out, O[0], O[1], O[2], O[3], O[4]);
  Comparator #(.Bits(5)) comparator_3 (.a(E), .b(driver_3_out), .eq(comparator_3_eq));  // open: gt, lt
  Comparator #(.Bits(5)) comparator_4 (.a(O), .b(driver_3_out), .eq(comparator_4_eq));  // open: gt, lt
  or or_4 (or_4_out, comparator_2_eq, comparator_1_eq);
  or or_5 (or_5_out, comparator_4_eq, comparator_3_eq);
  and and_1 (and_1_out, or_4_out, or_2_out);
  and and_2 (and_2_out, or_5_out, or_3_out);
  or or_6 (HOLD, and_1_out, and_2_out);
endmodule
