// Digital circuit RV32I-Registers.dig as structural Verilog
module RV32I_Registers (
  input  [31:0] D,
  input  C,
  input  [4:0] SEL,
  output [31:0] Q
);

  wire decoder_1_out_0, decoder_1_out_1, decoder_1_out_2, decoder_1_out_3, decoder_1_out_4, decoder_1_out_5,
       decoder_1_out_6, decoder_1_out_7, decoder_1_out_8, decoder_1_out_9, decoder_1_out_10,
       decoder_1_out_11, decoder_1_out_12, decoder_1_out_13, decoder_1_out_14, decoder_1_out_15,
       decoder_1_out_16, decoder_1_out_17, decoder_1_out_18, decoder_1_out_19, decoder_1_out_20,
       decoder_1_out_21, decoder_1_out_22, decoder_1_out_23, decoder_1_out_24, decoder_1_out_25,
       decoder_1_out_26, decoder_1_out_27, decoder_1_out_28, decoder_1_out_29, decoder_1_out_30,
       decoder_1_out_31;

  Decoder #(.Selector_Bits(5)) decoder_1 (
    .sel(SEL), .out_0(decoder_1_out_0), .out_1(decoder_1_out_1), .out_2(decoder_1_out_2),
    .out_3(decoder_1_out_3), .out_4(decoder_1_out_4), .out_5(decoder_1_out_5), .out_6(decoder_1_out_6),
    .out_7(decoder_1_out_7), .out_8(decoder_1_out_8), .out_9(decoder_1_out_9), .out_10(decoder_1_out_10),
    .out_11(decoder_1_out_11), .out_12(decoder_1_out_12), .out_13(decoder_1_out_13),
    .out_14(decoder_1_out_14), .out_15(decoder_1_out_15), .out_16(decoder_1_out_16),
    .out_17(decoder_1_out_17), .out_18(decoder_1_out_18), .out_19(decoder_1_out_19),
    .out_20(decoder_1_out_20), .out_21(decoder_1_out_21), .out_22(decoder_1_out_22),
    .out_23(decoder_1_out_23), .out_24(decoder_1_out_24), .out_25(decoder_1_out_25),
    .out_26(decoder_1_out_26), .out_27(decoder_1_out_27), .out_28(decoder_1_out_28),
    .out_29(decoder_1_out_29), .out_30(decoder_1_out_30), .out_31(decoder_1_out_31));
  assign Q = decoder_1_out_0 ? {32{1'b0}} : 32'bz;  // Driver driver_1
  Register #(.Bits(32)) x1 (.D(D), .C(C), .en(decoder_1_out_1), .Q(Q));
  Register #(.Bits(32)) x2 (.D(D), .C(C), .en(decoder_1_out_2), .Q(Q));
  Register #(.Bits(32)) x3 (.D(D), .C(C), .en(decoder_1_out_3), .Q(Q));
  Register #(.Bits(32)) x4 (.D(D), .C(C), .en(decoder_1_out_4), .Q(Q));
  Register #(.Bits(32)) x5 (.D(D), .C(C), .en(decoder_1_out_5), .Q(Q));
  Register #(.Bits(32)) x6 (.D(D), .C(C), .en(decoder_1_out_6), .Q(Q));
  Register #(.Bits(32)) x7 (.D(D), .C(C), .en(decoder_1_out_7), .Q(Q));
  Register #(.Bits(32)) x8 (.D(D), .C(C), .en(decoder_1_out_8), .Q(Q));
  Register #(.Bits(32)) x9 (.D(D), .C(C), .en(decoder_1_out_9), .Q(Q));
  Register #(.Bits(32)) x10 (.D(D), .C(C), .en(decoder_1_out_10), .Q(Q));
  Register #(.Bits(32)) x11 (.D(D), .C(C), .en(decoder_1_out_11), .Q(Q));
  Register #(.Bits(32)) x12 (.D(D), .C(C), .en(decoder_1_out_12), .Q(Q));
  Register #(.Bits(32)) x13 (.D(D), .C(C), .en(decoder_1_out_13), .Q(Q));
  Register #(.Bits(32)) x14 (.D(D), .C(C), .en(decoder_1_out_14), .Q(Q));
  Register #(.Bits(32)) x15 (.D(D), .C(C), .en(decoder_1_out_15), .Q(Q));
  Register #(.Bits(32)) x16 (.D(D), .C(C), .en(decoder_1_out_16), .Q(Q));
  Register #(.Bits(32)) x17 (.D(D), .C(C), .en(decoder_1_out_17), .Q(Q));
  Register #(.Bits(32)) x18 (.D(D), .C(C), .en(decoder_1_out_18), .Q(Q));
  Register #(.Bits(32)) x19 (.D(D), .C(C), .en(decoder_1_out_19), .Q(Q));
  Register #(.Bits(32)) x20 (.D(D), .C(C), .en(decoder_1_out_20), .Q(Q));
  Register #(.Bits(32)) x21 (.D(D), .C(C), .en(decoder_1_out_21), .Q(Q));
  Register #(.Bits(32)) x22 (.D(D), .C(C), .en(decoder_1_out_22), .Q(Q));
  Register #(.Bits(32)) x23 (.D(D), .C(C), .en(decoder_1_out_23), .Q(Q));
  Register #(.Bits(32)) x24 (.D(D), .C(C), .en(decoder_1_out_24), .Q(Q));
  Register #(.Bits(32)) x25 (.D(D), .C(C), .en(decoder_1_out_25), .Q(Q));
  Register #(.Bits(32)) x26 (.D(D), .C(C), .en(decoder_1_out_26), .Q(Q));
  Register #(.Bits(32)) x27 (.D(D), .C(C), .en(decoder_1_out_27), .Q(Q));
  Register #(.Bits(32)) x28 (.D(D), .C(C), .en(decoder_1_out_28), .Q(Q));
  Register #(.Bits(32)) x29 (.D(D), .C(C), .en(decoder_1_out_29), .Q(Q));
  Register #(.Bits(32)) x30 (.D(D), .C(C), .en(decoder_1_out_30), .Q(Q));
  Register #(.Bits(32)) x31 (.D(D), .C(C), .en(decoder_1_out_31), .Q(Q));
  // Pins of 1 and 5 bits meet at SEL
endmodule
