// Digital circuit RV32I-System.dig as structural Verilog
module RV32I_System (
  input  CLC
);

  wire _6_digit_display_1_d0, _6_digit_display_1_d1, _6_digit_display_1_d2, _6_digit_display_1_d3,
       _6_digit_display_1_d4, _6_digit_display_1_d5, _6_digit_display_2_d0, _6_digit_display_2_d1,
       _6_digit_display_2_d2, _6_digit_display_2_d3, _6_digit_display_2_d4, _6_digit_display_2_d5,
       _6_digit_display_3_d0, _6_digit_display_3_d1, _6_digit_display_3_d2, _6_digit_display_3_d3,
       _6_digit_display_3_d4, _6_digit_display_3_d5, _8_digit_display_1_d0, _8_digit_display_1_d1,
       _8_digit_display_1_d2, _8_digit_display_1_d3, _8_digit_display_1_d4, _8_digit_display_1_d5,
       _8_digit_display_1_d6, _8_digit_display_1_d7, _8_digit_display_2_d0, _8_digit_display_2_d1,
       _8_digit_display_2_d2, _8_digit_display_2_d3, _8_digit_display_2_d4, _8_digit_display_2_d5,
       _8_digit_display_2_d6, _8_digit_display_2_d7, _8_digit_display_3_d0, _8_digit_display_3_d1,
       _8_digit_display_3_d2, _8_digit_display_3_d3, _8_digit_display_3_d4, _8_digit_display_3_d5,
       _8_digit_display_3_d6, _8_digit_display_3_d7, _8_digit_display_4_d0, _8_digit_display_4_d1,
       _8_digit_display_4_d2, _8_digit_display_4_d3, _8_digit_display_4_d4, _8_digit_display_4_d5,
       _8_digit_display_4_d6, _8_digit_display_4_d7, _8_digit_display_5_d0, _8_digit_display_5_d1,
       _8_digit_display_5_d2, _8_digit_display_5_d3, _8_digit_display_5_d4, _8_digit_display_5_d5,
       _8_digit_display_5_d6, _8_digit_display_5_d7, _8_digit_display_6_d0, _8_digit_display_6_d1,
       _8_digit_display_6_d2, _8_digit_display_6_d3, _8_digit_display_6_d4, _8_digit_display_6_d5,
       _8_digit_display_6_d6, _8_digit_display_6_d7, _8_digit_display_7_d0, _8_digit_display_7_d1,
       _8_digit_display_7_d2, _8_digit_display_7_d3, _8_digit_display_7_d4, _8_digit_display_7_d5,
       _8_digit_display_7_d6, _8_digit_display_7_d7, _8_digit_display_8_d0, _8_digit_display_8_d1,
       _8_digit_display_8_d2, _8_digit_display_8_d3, _8_digit_display_8_d4, _8_digit_display_8_d5,
       _8_digit_display_8_d6, _8_digit_display_8_d7, _8_digit_display_9_d0, _8_digit_display_9_d1,
       _8_digit_display_9_d2, _8_digit_display_9_d3, _8_digit_display_9_d4, _8_digit_display_9_d5,
       _8_digit_display_9_d6, _8_digit_display_9_d7, and_1_out, binary_bcd_converter_1_d0,
       binary_bcd_converter_1_d1, binary_bcd_converter_2_d0, binary_bcd_converter_2_d1, BOOT_CNT_EN,
       BOOT_CNT_SET_MEM_ADDR, BOOT_COMPLETE, BOOT_COUNTER_OVERFLOW, COMP, CPU_cpu_set_mem_address,
       CPU_cpu_write_mem, CPU_error, GO, NORMAL, not_1_out, or_1_out, P_out, R_out, ROM_WRITE_MEM, RUN,
       rv32i_instruction_display_1_d0, rv32i_instruction_display_1_d1, rv32i_instruction_display_1_d2,
       rv32i_instruction_display_1_d3, rv32i_instruction_display_1_d4, rv32i_instruction_display_1_d5,
       rv32i_instruction_display_1_d6, rv32i_instruction_display_1_d7, rv32i_instruction_display_2_d0,
       rv32i_instruction_display_2_d1, rv32i_instruction_display_2_d2, rv32i_instruction_display_2_d3,
       rv32i_instruction_display_2_d4, rv32i_instruction_display_2_d5, rv32i_instruction_display_2_d6,
       rv32i_instruction_display_2_d7, rv32i_instruction_display_3_d0, rv32i_instruction_display_3_d1,
       rv32i_instruction_display_3_d2, rv32i_instruction_display_3_d3, rv32i_instruction_display_3_d4,
       rv32i_instruction_display_3_d5, rv32i_instruction_display_3_d6, rv32i_instruction_display_3_d7,
       rv32i_instruction_display_4_d0, rv32i_instruction_display_4_d1, rv32i_instruction_display_4_d2,
       rv32i_instruction_display_4_d3, rv32i_instruction_display_4_d4, rv32i_instruction_display_4_d5,
       rv32i_instruction_display_4_d6, rv32i_instruction_display_4_d7, S_out, T_out;
  wire [3:0] _6_digit_display_1__0, _6_digit_display_1__1, _6_digit_display_1__2, _6_digit_display_1__3,
       _6_digit_display_1__4, _6_digit_display_1__5, _6_digit_display_2__0, _6_digit_display_2__1,
       _6_digit_display_2__2, _6_digit_display_2__3, _6_digit_display_2__4, _6_digit_display_2__5,
       _6_digit_display_3__0, _6_digit_display_3__1, _6_digit_display_3__2, _6_digit_display_3__3,
       _6_digit_display_3__4, _6_digit_display_3__5, _8_digit_display_1__0, _8_digit_display_1__1,
       _8_digit_display_1__2, _8_digit_display_1__3, _8_digit_display_1__4, _8_digit_display_1__5,
       _8_digit_display_1__6, _8_digit_display_1__7, _8_digit_display_2__0, _8_digit_display_2__1,
       _8_digit_display_2__2, _8_digit_display_2__3, _8_digit_display_2__4, _8_digit_display_2__5,
       _8_digit_display_2__6, _8_digit_display_2__7, _8_digit_display_3__0, _8_digit_display_3__1,
       _8_digit_display_3__2, _8_digit_display_3__3, _8_digit_display_3__4, _8_digit_display_3__5,
       _8_digit_display_3__6, _8_digit_display_3__7, _8_digit_display_4__0, _8_digit_display_4__1,
       _8_digit_display_4__2, _8_digit_display_4__3, _8_digit_display_4__4, _8_digit_display_4__5,
       _8_digit_display_4__6, _8_digit_display_4__7, _8_digit_display_5__0, _8_digit_display_5__1,
       _8_digit_display_5__2, _8_digit_display_5__3, _8_digit_display_5__4, _8_digit_display_5__5,
       _8_digit_display_5__6, _8_digit_display_5__7, _8_digit_display_6__0, _8_digit_display_6__1,
       _8_digit_display_6__2, _8_digit_display_6__3, _8_digit_display_6__4, _8_digit_display_6__5,
       _8_digit_display_6__6, _8_digit_display_6__7, _8_digit_display_7__0, _8_digit_display_7__1,
       _8_digit_display_7__2, _8_digit_display_7__3, _8_digit_display_7__4, _8_digit_display_7__5,
       _8_digit_display_7__6, _8_digit_display_7__7, _8_digit_display_8__0, _8_digit_display_8__1,
       _8_digit_display_8__2, _8_digit_display_8__3, _8_digit_display_8__4, _8_digit_display_8__5,
       _8_digit_display_8__6, _8_digit_display_8__7, _8_digit_display_9__0, _8_digit_display_9__1,
       _8_digit_display_9__2, _8_digit_display_9__3, _8_digit_display_9__4, _8_digit_display_9__5,
       _8_digit_display_9__6, _8_digit_display_9__7, binary_bcd_converter_1__0, binary_bcd_converter_1__1,
       binary_bcd_converter_2__0, binary_bcd_converter_2__1;
  wire [4:0] HELD_REGISTER_0, HELD_REGISTER_1;
  wire [7:0] ALU_INSTR;
  wire [15:0] rv32i_instruction_display_1__0, rv32i_instruction_display_1__1, rv32i_instruction_display_1__2,
       rv32i_instruction_display_1__3, rv32i_instruction_display_1__4, rv32i_instruction_display_1__5,
       rv32i_instruction_display_1__6, rv32i_instruction_display_1__7, rv32i_instruction_display_2__0,
       rv32i_instruction_display_2__1, rv32i_instruction_display_2__2, rv32i_instruction_display_2__3,
       rv32i_instruction_display_2__4, rv32i_instruction_display_2__5, rv32i_instruction_display_2__6,
       rv32i_instruction_display_2__7, rv32i_instruction_display_3__0, rv32i_instruction_display_3__1,
       rv32i_instruction_display_3__2, rv32i_instruction_display_3__3, rv32i_instruction_display_3__4,
       rv32i_instruction_display_3__5, rv32i_instruction_display_3__6, rv32i_instruction_display_3__7,
       rv32i_instruction_display_4__0, rv32i_instruction_display_4__1, rv32i_instruction_display_4__2,
       rv32i_instruction_display_4__3, rv32i_instruction_display_4__4, rv32i_instruction_display_4__5,
       rv32i_instruction_display_4__6, rv32i_instruction_display_4__7;
  wire [23:0] BOOT_CNT, CPU_mem_address, MEM_R_W_A, PC_OUT;
  wire [31:0] ALU_A, ALU_B, ALU_Y, counter_1_out, counter_2_out, CPU_mem_w, INSTR_DECODE, INSTR_EXECUTE,
       INSTR_MEMORY, INSTR_WRITE, MEM_R_W, ROM;

  and and_1 (and_1_out, GO, RUN);
  Seven_Seg_Hex seven_seg_hex_1 (.d(_8_digit_display_1__0), .dp(_8_digit_display_1_d0));
  Counter #(.Bits(24)) u_BOOT_CNT (
    .en(BOOT_CNT_EN), .C(CLC), .clr(NORMAL), .out(BOOT_CNT), .ovf(BOOT_COUNTER_OVERFLOW));
  LED led_1 (.in(NORMAL));
  LED led_2 (.in(RUN));
  Seven_Seg_Hex seven_seg_hex_2 (.d(_6_digit_display_1__0), .dp(_6_digit_display_1_d0));
  LED led_3 (.in(GO));
  Seven_Seg_Hex seven_seg_hex_3 (.d(_8_digit_display_1__1), .dp(_8_digit_display_1_d1));
  Seven_Seg_Hex seven_seg_hex_4 (.d(_8_digit_display_1__2), .dp(_8_digit_display_1_d2));
  _8_Digit_Display _8_digit_display_1 (
    .I(ROM), ._0(_8_digit_display_1__0), .D0(_8_digit_display_1_d0), ._1(_8_digit_display_1__1),
    .D1(_8_digit_display_1_d1), ._2(_8_digit_display_1__2), .D2(_8_digit_display_1_d2),
    ._3(_8_digit_display_1__3), .D3(_8_digit_display_1_d3), ._4(_8_digit_display_1__4),
    .D4(_8_digit_display_1_d4), ._5(_8_digit_display_1__5), .D5(_8_digit_display_1_d5),
    ._6(_8_digit_display_1__6), .D6(_8_digit_display_1_d6), ._7(_8_digit_display_1__7),
    .D7(_8_digit_display_1_d7));
  Counter #(.Bits(32)) counter_1 (.en(and_1_out), .C(CLC), .clr(1'b0), .out(counter_1_out));  // open: ovf
  Counter #(.Bits(32)) counter_2 (.en(RUN), .C(CLC), .clr(1'b0), .out(counter_2_out));  // open: ovf
  Button S (.out(S_out));
  Button R (.out(R_out));
  Button T (.out(T_out));
  Seven_Seg_Hex seven_seg_hex_5 (.d(_6_digit_display_1__1), .dp(_6_digit_display_1_d1));
  Seven_Seg_Hex seven_seg_hex_6 (.d(_6_digit_display_1__2), .dp(_6_digit_display_1_d2));
  Seven_Seg_Hex seven_seg_hex_7 (.d(_8_digit_display_1__3), .dp(_8_digit_display_1_d3));
  Seven_Seg_Hex seven_seg_hex_8 (.d(_8_digit_display_1__4), .dp(_8_digit_display_1_d4));
  _6_Digit_Display _6_digit_display_1 (
    .I(BOOT_CNT), ._0(_6_digit_display_1__0), .D0(_6_digit_display_1_d0), ._1(_6_digit_display_1__1),
    .D1(_6_digit_display_1_d1), ._2(_6_digit_display_1__2), .D2(_6_digit_display_1_d2),
    ._3(_6_digit_display_1__3), .D3(_6_digit_display_1_d3), ._4(_6_digit_display_1__4),
    .D4(_6_digit_display_1_d4), ._5(_6_digit_display_1__5), .D5(_6_digit_display_1_d5));
  Button P (.out(P_out));
  Seven_Seg_Hex seven_seg_hex_9 (.d(_6_digit_display_1__3), .dp(_6_digit_display_1_d3));
  Seven_Seg_Hex seven_seg_hex_10 (.d(_6_digit_display_1__4), .dp(_6_digit_display_1_d4));
  Seven_Seg_Hex seven_seg_hex_11 (.d(_8_digit_display_1__5), .dp(_8_digit_display_1_d5));
  Seven_Seg_Hex seven_seg_hex_12 (.d(_8_digit_display_1__6), .dp(_8_digit_display_1_d6));
  RV32I_Control rv32i_control_1 (
    .START(S_out), .PAUSE(P_out), .RESET(R_out), .BC(BOOT_COMPLETE), .BCO(BOOT_COUNTER_OVERFLOW), .CLC(CLC),
    .RUN_OVERRIDE(T_out), .NORMAL(NORMAL), .RUN(RUN), .BCE(BOOT_CNT_EN),
    .BC_SET_R_W_A(BOOT_CNT_SET_MEM_ADDR), .ROM_SET_MEM_R_W(ROM_WRITE_MEM));
  Seven_Seg_Hex seven_seg_hex_13 (.d(_6_digit_display_1__5), .dp(_6_digit_display_1_d5));
  Seven_Seg_Hex seven_seg_hex_14 (.d(_8_digit_display_1__7), .dp(_8_digit_display_1_d7));
  ROM #(.AddrBits(24), .isProgramMemory("true"), .Bits(32)) u_ROM (.A(BOOT_CNT), .sel(1'b1), .D(ROM));
  Comparator #(.Bits(24)) comparator_1 (.a(BOOT_CNT), .b(24'h60), .eq(BOOT_COMPLETE));  // open: gt, lt
  Seven_Seg_Hex seven_seg_hex_15 (.d(_8_digit_display_2__0), .dp(_8_digit_display_2_d0));
  Seven_Seg_Hex seven_seg_hex_16 (.d(_8_digit_display_2__1), .dp(_8_digit_display_2_d1));
  SixteenSeg sixteenseg_1 (.led(rv32i_instruction_display_1__0), .dp(rv32i_instruction_display_1_d0));
  SixteenSeg sixteenseg_2 (.led(rv32i_instruction_display_1__1), .dp(rv32i_instruction_display_1_d1));
  _8_Digit_Display _8_digit_display_2 (
    .I(INSTR_DECODE), ._0(_8_digit_display_2__0), .D0(_8_digit_display_2_d0), ._1(_8_digit_display_2__1),
    .D1(_8_digit_display_2_d1), ._2(_8_digit_display_2__2), .D2(_8_digit_display_2_d2),
    ._3(_8_digit_display_2__3), .D3(_8_digit_display_2_d3), ._4(_8_digit_display_2__4),
    .D4(_8_digit_display_2_d4), ._5(_8_digit_display_2__5), .D5(_8_digit_display_2_d5),
    ._6(_8_digit_display_2__6), .D6(_8_digit_display_2_d6), ._7(_8_digit_display_2__7),
    .D7(_8_digit_display_2_d7));
  RV32I_Instruction_Display rv32i_instruction_display_1 (
    .INSTR(INSTR_DECODE), ._0(rv32i_instruction_display_1__0), .D0(rv32i_instruction_display_1_d0),
    ._1(rv32i_instruction_display_1__1), .D1(rv32i_instruction_display_1_d1),
    ._2(rv32i_instruction_display_1__2), .D2(rv32i_instruction_display_1_d2),
    ._3(rv32i_instruction_display_1__3), .D3(rv32i_instruction_display_1_d3),
    ._4(rv32i_instruction_display_1__4), .D4(rv32i_instruction_display_1_d4),
    ._5(rv32i_instruction_display_1__5), .D5(rv32i_instruction_display_1_d5),
    ._6(rv32i_instruction_display_1__6), .D6(rv32i_instruction_display_1_d6),
    ._7(rv32i_instruction_display_1__7), .D7(rv32i_instruction_display_1_d7));
  Seven_Seg_Hex seven_seg_hex_17 (.d(binary_bcd_converter_1__0), .dp(binary_bcd_converter_1_d0));
  Seven_Seg_Hex seven_seg_hex_18 (.d(_6_digit_display_2__0), .dp(_6_digit_display_2_d0));
  Seven_Seg_Hex seven_seg_hex_19 (.d(_6_digit_display_2__1), .dp(_6_digit_display_2_d1));
  Seven_Seg_Hex seven_seg_hex_20 (.d(_8_digit_display_2__2), .dp(_8_digit_display_2_d2));
  Seven_Seg_Hex seven_seg_hex_21 (.d(_8_digit_display_2__3), .dp(_8_digit_display_2_d3));
  _6_Digit_Display _6_digit_display_2 (
    .I(PC_OUT), ._0(_6_digit_display_2__0), .D0(_6_digit_display_2_d0), ._1(_6_digit_display_2__1),
    .D1(_6_digit_display_2_d1), ._2(_6_digit_display_2__2), .D2(_6_digit_display_2_d2),
    ._3(_6_digit_display_2__3), .D3(_6_digit_display_2_d3), ._4(_6_digit_display_2__4),
    .D4(_6_digit_display_2_d4), ._5(_6_digit_display_2__5), .D5(_6_digit_display_2_d5));
  SixteenSeg sixteenseg_3 (.led(rv32i_instruction_display_1__2), .dp(rv32i_instruction_display_1_d2));
  SixteenSeg sixteenseg_4 (.led(rv32i_instruction_display_1__3), .dp(rv32i_instruction_display_1_d3));
  Seven_Seg_Hex seven_seg_hex_22 (.d(binary_bcd_converter_1__1), .dp(binary_bcd_converter_1_d1));
  Seven_Seg_Hex seven_seg_hex_23 (.d(_6_digit_display_2__2), .dp(_6_digit_display_2_d2));
  Seven_Seg_Hex seven_seg_hex_24 (.d(_6_digit_display_2__3), .dp(_6_digit_display_2_d3));
  Binary_BCD_Converter binary_bcd_converter_1 (
    .I(HELD_REGISTER_1), ._0(binary_bcd_converter_1__0), .D0(binary_bcd_converter_1_d0),
    ._1(binary_bcd_converter_1__1), .D1(binary_bcd_converter_1_d1));
  Seven_Seg_Hex seven_seg_hex_25 (.d(_8_digit_display_2__4), .dp(_8_digit_display_2_d4));
  Seven_Seg_Hex seven_seg_hex_26 (.d(_8_digit_display_2__5), .dp(_8_digit_display_2_d5));
  SixteenSeg sixteenseg_5 (.led(rv32i_instruction_display_1__4), .dp(rv32i_instruction_display_1_d4));
  SixteenSeg sixteenseg_6 (.led(rv32i_instruction_display_1__5), .dp(rv32i_instruction_display_1_d5));
  Seven_Seg_Hex seven_seg_hex_27 (.d(binary_bcd_converter_2__0), .dp(binary_bcd_converter_2_d0));
  Seven_Seg_Hex seven_seg_hex_28 (.d(binary_bcd_converter_2__1), .dp(binary_bcd_converter_2_d1));
  Seven_Seg_Hex seven_seg_hex_29 (.d(_6_digit_display_2__4), .dp(_6_digit_display_2_d4));
  Seven_Seg_Hex seven_seg_hex_30 (.d(_6_digit_display_2__5), .dp(_6_digit_display_2_d5));
  Binary_BCD_Converter binary_bcd_converter_2 (
    .I(HELD_REGISTER_0), ._0(binary_bcd_converter_2__0), .D0(binary_bcd_converter_2_d0),
    ._1(binary_bcd_converter_2__1), .D1(binary_bcd_converter_2_d1));
  Seven_Seg_Hex seven_seg_hex_31 (.d(_8_digit_display_2__6), .dp(_8_digit_display_2_d6));
  Seven_Seg_Hex seven_seg_hex_32 (.d(_8_digit_display_2__7), .dp(_8_digit_display_2_d7));
  SixteenSeg sixteenseg_7 (.led(rv32i_instruction_display_1__6), .dp(rv32i_instruction_display_1_d6));
  SixteenSeg sixteenseg_8 (.led(rv32i_instruction_display_1__7), .dp(rv32i_instruction_display_1_d7));
  Seven_Seg_Hex seven_seg_hex_33 (.d(_8_digit_display_3__0), .dp(_8_digit_display_3_d0));
  Seven_Seg_Hex seven_seg_hex_34 (.d(_8_digit_display_4__0), .dp(_8_digit_display_4_d0));
  Seven_Seg_Hex seven_seg_hex_35 (.d(_8_digit_display_5__0), .dp(_8_digit_display_5_d0));
  Seven_Seg_Hex seven_seg_hex_36 (.d(_8_digit_display_6__0), .dp(_8_digit_display_6_d0));
  SixteenSeg sixteenseg_9 (.led(rv32i_instruction_display_2__0), .dp(rv32i_instruction_display_2_d0));
  Seven_Seg_Hex seven_seg_hex_37 (.d(_8_digit_display_3__1), .dp(_8_digit_display_3_d1));
  Seven_Seg_Hex seven_seg_hex_38 (.d(_8_digit_display_3__2), .dp(_8_digit_display_3_d2));
  Seven_Seg_Hex seven_seg_hex_39 (.d(_8_digit_display_4__1), .dp(_8_digit_display_4_d1));
  Seven_Seg_Hex seven_seg_hex_40 (.d(_8_digit_display_4__2), .dp(_8_digit_display_4_d2));
  _8_Digit_Display _8_digit_display_3 (
    .I(ALU_A), ._0(_8_digit_display_3__0), .D0(_8_digit_display_3_d0), ._1(_8_digit_display_3__1),
    .D1(_8_digit_display_3_d1), ._2(_8_digit_display_3__2), .D2(_8_digit_display_3_d2),
    ._3(_8_digit_display_3__3), .D3(_8_digit_display_3_d3), ._4(_8_digit_display_3__4),
    .D4(_8_digit_display_3_d4), ._5(_8_digit_display_3__5), .D5(_8_digit_display_3_d5),
    ._6(_8_digit_display_3__6), .D6(_8_digit_display_3_d6), ._7(_8_digit_display_3__7),
    .D7(_8_digit_display_3_d7));
  Seven_Seg_Hex seven_seg_hex_41 (.d(_8_digit_display_5__1), .dp(_8_digit_display_5_d1));
  Seven_Seg_Hex seven_seg_hex_42 (.d(_8_digit_display_5__2), .dp(_8_digit_display_5_d2));
  _8_Digit_Display _8_digit_display_4 (
    .I(ALU_B), ._0(_8_digit_display_4__0), .D0(_8_digit_display_4_d0), ._1(_8_digit_display_4__1),
    .D1(_8_digit_display_4_d1), ._2(_8_digit_display_4__2), .D2(_8_digit_display_4_d2),
    ._3(_8_digit_display_4__3), .D3(_8_digit_display_4_d3), ._4(_8_digit_display_4__4),
    .D4(_8_digit_display_4_d4), ._5(_8_digit_display_4__5), .D5(_8_digit_display_4_d5),
    ._6(_8_digit_display_4__6), .D6(_8_digit_display_4_d6), ._7(_8_digit_display_4__7),
    .D7(_8_digit_display_4_d7));
  Seven_Seg_Hex seven_seg_hex_43 (.d(_8_digit_display_6__1), .dp(_8_digit_display_6_d1));
  Seven_Seg_Hex seven_seg_hex_44 (.d(_8_digit_display_6__2), .dp(_8_digit_display_6_d2));
  _8_Digit_Display _8_digit_display_5 (
    .I(ALU_Y), ._0(_8_digit_display_5__0), .D0(_8_digit_display_5_d0), ._1(_8_digit_display_5__1),
    .D1(_8_digit_display_5_d1), ._2(_8_digit_display_5__2), .D2(_8_digit_display_5_d2),
    ._3(_8_digit_display_5__3), .D3(_8_digit_display_5_d3), ._4(_8_digit_display_5__4),
    .D4(_8_digit_display_5_d4), ._5(_8_digit_display_5__5), .D5(_8_digit_display_5_d5),
    ._6(_8_digit_display_5__6), .D6(_8_digit_display_5_d6), ._7(_8_digit_display_5__7),
    .D7(_8_digit_display_5_d7));
  SixteenSeg sixteenseg_10 (.led(rv32i_instruction_display_2__1), .dp(rv32i_instruction_display_2_d1));
  SixteenSeg sixteenseg_11 (.led(rv32i_instruction_display_2__2), .dp(rv32i_instruction_display_2_d2));
  _8_Digit_Display _8_digit_display_6 (
    .I(INSTR_EXECUTE), ._0(_8_digit_display_6__0), .D0(_8_digit_display_6_d0), ._1(_8_digit_display_6__1),
    .D1(_8_digit_display_6_d1), ._2(_8_digit_display_6__2), .D2(_8_digit_display_6_d2),
    ._3(_8_digit_display_6__3), .D3(_8_digit_display_6_d3), ._4(_8_digit_display_6__4),
    .D4(_8_digit_display_6_d4), ._5(_8_digit_display_6__5), .D5(_8_digit_display_6_d5),
    ._6(_8_digit_display_6__6), .D6(_8_digit_display_6_d6), ._7(_8_digit_display_6__7),
    .D7(_8_digit_display_6_d7));
  RV32I_Instruction_Display rv32i_instruction_display_2 (
    .INSTR(INSTR_EXECUTE), ._0(rv32i_instruction_display_2__0), .D0(rv32i_instruction_display_2_d0),
    ._1(rv32i_instruction_display_2__1), .D1(rv32i_instruction_display_2_d1),
    ._2(rv32i_instruction_display_2__2), .D2(rv32i_instruction_display_2_d2),
    ._3(rv32i_instruction_display_2__3), .D3(rv32i_instruction_display_2_d3),
    ._4(rv32i_instruction_display_2__4), .D4(rv32i_instruction_display_2_d4),
    ._5(rv32i_instruction_display_2__5), .D5(rv32i_instruction_display_2_d5),
    ._6(rv32i_instruction_display_2__6), .D6(rv32i_instruction_display_2_d6),
    ._7(rv32i_instruction_display_2__7), .D7(rv32i_instruction_display_2_d7));
  Seven_Seg_Hex seven_seg_hex_45 (.d(_8_digit_display_3__3), .dp(_8_digit_display_3_d3));
  Seven_Seg_Hex seven_seg_hex_46 (.d(_8_digit_display_3__4), .dp(_8_digit_display_3_d4));
  Seven_Seg_Hex seven_seg_hex_47 (.d(_8_digit_display_4__3), .dp(_8_digit_display_4_d3));
  Seven_Seg_Hex seven_seg_hex_48 (.d(_8_digit_display_4__4), .dp(_8_digit_display_4_d4));
  Seven_Seg_Hex seven_seg_hex_49 (.d(_8_digit_display_5__3), .dp(_8_digit_display_5_d3));
  Seven_Seg_Hex seven_seg_hex_50 (.d(_8_digit_display_5__4), .dp(_8_digit_display_5_d4));
  Seven_Seg_Hex seven_seg_hex_51 (.d(_8_digit_display_6__3), .dp(_8_digit_display_6_d3));
  Seven_Seg_Hex seven_seg_hex_52 (.d(_8_digit_display_6__4), .dp(_8_digit_display_6_d4));
  SixteenSeg sixteenseg_12 (.led(rv32i_instruction_display_2__3), .dp(rv32i_instruction_display_2_d3));
  SixteenSeg sixteenseg_13 (.led(rv32i_instruction_display_2__4), .dp(rv32i_instruction_display_2_d4));
  Seven_Seg_Hex seven_seg_hex_53 (.d(_8_digit_display_3__5), .dp(_8_digit_display_3_d5));
  Seven_Seg_Hex seven_seg_hex_54 (.d(_8_digit_display_3__6), .dp(_8_digit_display_3_d6));
  Seven_Seg_Hex seven_seg_hex_55 (.d(_8_digit_display_4__5), .dp(_8_digit_display_4_d5));
  Seven_Seg_Hex seven_seg_hex_56 (.d(_8_digit_display_4__6), .dp(_8_digit_display_4_d6));
  Seven_Seg_Hex seven_seg_hex_57 (.d(_8_digit_display_5__5), .dp(_8_digit_display_5_d5));
  Seven_Seg_Hex seven_seg_hex_58 (.d(_8_digit_display_5__6), .dp(_8_digit_display_5_d6));
  Seven_Seg_Hex seven_seg_hex_59 (.d(_8_digit_display_6__5), .dp(_8_digit_display_6_d5));
  Seven_Seg_Hex seven_seg_hex_60 (.d(_8_digit_display_6__6), .dp(_8_digit_display_6_d6));
  SixteenSeg sixteenseg_14 (.led(rv32i_instruction_display_2__5), .dp(rv32i_instruction_display_2_d5));
  SixteenSeg sixteenseg_15 (.led(rv32i_instruction_display_2__6), .dp(rv32i_instruction_display_2_d6));
  Seven_Seg_Hex seven_seg_hex_61 (.d(_8_digit_display_3__7), .dp(_8_digit_display_3_d7));
  Seven_Seg_Hex seven_seg_hex_62 (.d(_8_digit_display_4__7), .dp(_8_digit_display_4_d7));
  Seven_Seg_Hex seven_seg_hex_63 (.d(_8_digit_display_5__7), .dp(_8_digit_display_5_d7));
  Seven_Seg_Hex seven_seg_hex_64 (.d(_8_digit_display_6__7), .dp(_8_digit_display_6_d7));
  SixteenSeg sixteenseg_16 (.led(rv32i_instruction_display_2__7), .dp(rv32i_instruction_display_2_d7));
  or or_1 (or_1_out, ~NORMAL, CPU_cpu_write_mem);  // Or
  Seven_Seg_Hex seven_seg_hex_65 (.d(_8_digit_display_7__0), .dp(_8_digit_display_7_d0));
  Seven_Seg_Hex seven_seg_hex_66 (.d(_8_digit_display_7__1), .dp(_8_digit_display_7_d1));
  _8_Digit_Display _8_digit_display_7 (
    .I(MEM_R_W), ._0(_8_digit_display_7__0), .D0(_8_digit_display_7_d0), ._1(_8_digit_display_7__1),
    .D1(_8_digit_display_7_d1), ._2(_8_digit_display_7__2), .D2(_8_digit_display_7_d2),
    ._3(_8_digit_display_7__3), .D3(_8_digit_display_7_d3), ._4(_8_digit_display_7__4),
    .D4(_8_digit_display_7_d4), ._5(_8_digit_display_7__5), .D5(_8_digit_display_7_d5),
    ._6(_8_digit_display_7__6), .D6(_8_digit_display_7_d6), ._7(_8_digit_display_7__7),
    .D7(_8_digit_display_7_d7));
  Seven_Seg_Hex seven_seg_hex_67 (.d(_8_digit_display_8__0), .dp(_8_digit_display_8_d0));
  Seven_Seg_Hex seven_seg_hex_68 (.d(_8_digit_display_8__1), .dp(_8_digit_display_8_d1));
  SixteenSeg sixteenseg_17 (.led(rv32i_instruction_display_3__0), .dp(rv32i_instruction_display_3_d0));
  SixteenSeg sixteenseg_18 (.led(rv32i_instruction_display_3__1), .dp(rv32i_instruction_display_3_d1));
  _8_Digit_Display _8_digit_display_8 (
    .I(INSTR_MEMORY), ._0(_8_digit_display_8__0), .D0(_8_digit_display_8_d0), ._1(_8_digit_display_8__1),
    .D1(_8_digit_display_8_d1), ._2(_8_digit_display_8__2), .D2(_8_digit_display_8_d2),
    ._3(_8_digit_display_8__3), .D3(_8_digit_display_8_d3), ._4(_8_digit_display_8__4),
    .D4(_8_digit_display_8_d4), ._5(_8_digit_display_8__5), .D5(_8_digit_display_8_d5),
    ._6(_8_digit_display_8__6), .D6(_8_digit_display_8_d6), ._7(_8_digit_display_8__7),
    .D7(_8_digit_display_8_d7));
  RV32I_Instruction_Display rv32i_instruction_display_3 (
    .INSTR(INSTR_MEMORY), ._0(rv32i_instruction_display_3__0), .D0(rv32i_instruction_display_3_d0),
    ._1(rv32i_instruction_display_3__1), .D1(rv32i_instruction_display_3_d1),
    ._2(rv32i_instruction_display_3__2), .D2(rv32i_instruction_display_3_d2),
    ._3(rv32i_instruction_display_3__3), .D3(rv32i_instruction_display_3_d3),
    ._4(rv32i_instruction_display_3__4), .D4(rv32i_instruction_display_3_d4),
    ._5(rv32i_instruction_display_3__5), .D5(rv32i_instruction_display_3_d5),
    ._6(rv32i_instruction_display_3__6), .D6(rv32i_instruction_display_3_d6),
    ._7(rv32i_instruction_display_3__7), .D7(rv32i_instruction_display_3_d7));
  Seven_Seg_Hex seven_seg_hex_69 (.d(_6_digit_display_3__0), .dp(_6_digit_display_3_d0));
  Seven_Seg_Hex seven_seg_hex_70 (.d(_6_digit_display_3__1), .dp(_6_digit_display_3_d1));
  Seven_Seg_Hex seven_seg_hex_71 (.d(_8_digit_display_7__2), .dp(_8_digit_display_7_d2));
  Seven_Seg_Hex seven_seg_hex_72 (.d(_8_digit_display_7__3), .dp(_8_digit_display_7_d3));
  _6_Digit_Display _6_digit_display_3 (
    .I(MEM_R_W_A), ._0(_6_digit_display_3__0), .D0(_6_digit_display_3_d0), ._1(_6_digit_display_3__1),
    .D1(_6_digit_display_3_d1), ._2(_6_digit_display_3__2), .D2(_6_digit_display_3_d2),
    ._3(_6_digit_display_3__3), .D3(_6_digit_display_3_d3), ._4(_6_digit_display_3__4),
    .D4(_6_digit_display_3_d4), ._5(_6_digit_display_3__5), .D5(_6_digit_display_3_d5));
  Seven_Seg_Hex seven_seg_hex_73 (.d(_8_digit_display_8__2), .dp(_8_digit_display_8_d2));
  Seven_Seg_Hex seven_seg_hex_74 (.d(_8_digit_display_8__3), .dp(_8_digit_display_8_d3));
  SixteenSeg sixteenseg_19 (.led(rv32i_instruction_display_3__2), .dp(rv32i_instruction_display_3_d2));
  SixteenSeg sixteenseg_20 (.led(rv32i_instruction_display_3__3), .dp(rv32i_instruction_display_3_d3));
  assign MEM_R_W_A = BOOT_CNT_SET_MEM_ADDR ? BOOT_CNT : 24'bz;  // Driver driver_1
  assign MEM_R_W_A = CPU_cpu_set_mem_address ? CPU_mem_address : 24'bz;  // Driver driver_2
  Seven_Seg_Hex seven_seg_hex_75 (.d(_6_digit_display_3__2), .dp(_6_digit_display_3_d2));
  Seven_Seg_Hex seven_seg_hex_76 (.d(_6_digit_display_3__3), .dp(_6_digit_display_3_d3));
  Seven_Seg_Hex seven_seg_hex_77 (.d(_8_digit_display_7__4), .dp(_8_digit_display_7_d4));
  Seven_Seg_Hex seven_seg_hex_78 (.d(_8_digit_display_7__5), .dp(_8_digit_display_7_d5));
  Seven_Seg_Hex seven_seg_hex_79 (.d(_8_digit_display_8__4), .dp(_8_digit_display_8_d4));
  Seven_Seg_Hex seven_seg_hex_80 (.d(_8_digit_display_8__5), .dp(_8_digit_display_8_d5));
  SixteenSeg sixteenseg_21 (.led(rv32i_instruction_display_3__4), .dp(rv32i_instruction_display_3_d4));
  SixteenSeg sixteenseg_22 (.led(rv32i_instruction_display_3__5), .dp(rv32i_instruction_display_3_d5));
  not not_1 (not_1_out, or_1_out);
  PullDown #(.Bits(24)) pulldown_1 (.out(MEM_R_W_A));
  Seven_Seg_Hex seven_seg_hex_81 (.d(_6_digit_display_3__4), .dp(_6_digit_display_3_d4));
  Seven_Seg_Hex seven_seg_hex_82 (.d(_6_digit_display_3__5), .dp(_6_digit_display_3_d5));
  Seven_Seg_Hex seven_seg_hex_83 (.d(_8_digit_display_7__6), .dp(_8_digit_display_7_d6));
  Seven_Seg_Hex seven_seg_hex_84 (.d(_8_digit_display_7__7), .dp(_8_digit_display_7_d7));
  Seven_Seg_Hex seven_seg_hex_85 (.d(_8_digit_display_8__6), .dp(_8_digit_display_8_d6));
  Seven_Seg_Hex seven_seg_hex_86 (.d(_8_digit_display_8__7), .dp(_8_digit_display_8_d7));
  SixteenSeg sixteenseg_23 (.led(rv32i_instruction_display_3__6), .dp(rv32i_instruction_display_3_d6));
  SixteenSeg sixteenseg_24 (.led(rv32i_instruction_display_3__7), .dp(rv32i_instruction_display_3_d7));
  RAMDualAccess #(.AddrBits(24), .isProgramMemory("true"), .Bits(32)) Memory (
    .str(or_1_out), .C(CLC), .ld(not_1_out), .A1(MEM_R_W_A), .Din1(MEM_R_W), .A2(PC_OUT), .D1(MEM_R_W),
    .D2(INSTR_DECODE));
  Seven_Seg_Hex seven_seg_hex_87 (.d(_8_digit_display_9__0), .dp(_8_digit_display_9_d0));
  SixteenSeg sixteenseg_25 (.led(rv32i_instruction_display_4__0), .dp(rv32i_instruction_display_4_d0));
  assign MEM_R_W = CPU_cpu_write_mem ? CPU_mem_w : 32'bz;  // Driver driver_3
  assign MEM_R_W = ROM_WRITE_MEM ? ROM : 32'bz;  // Driver driver_4
  Seven_Seg_Hex seven_seg_hex_88 (.d(_8_digit_display_9__1), .dp(_8_digit_display_9_d1));
  Seven_Seg_Hex seven_seg_hex_89 (.d(_8_digit_display_9__2), .dp(_8_digit_display_9_d2));
  SixteenSeg sixteenseg_26 (.led(rv32i_instruction_display_4__1), .dp(rv32i_instruction_display_4_d1));
  SixteenSeg sixteenseg_27 (.led(rv32i_instruction_display_4__2), .dp(rv32i_instruction_display_4_d2));
  _8_Digit_Display _8_digit_display_9 (
    .I(INSTR_WRITE), ._0(_8_digit_display_9__0), .D0(_8_digit_display_9_d0), ._1(_8_digit_display_9__1),
    .D1(_8_digit_display_9_d1), ._2(_8_digit_display_9__2), .D2(_8_digit_display_9_d2),
    ._3(_8_digit_display_9__3), .D3(_8_digit_display_9_d3), ._4(_8_digit_display_9__4),
    .D4(_8_digit_display_9_d4), ._5(_8_digit_display_9__5), .D5(_8_digit_display_9_d5),
    ._6(_8_digit_display_9__6), .D6(_8_digit_display_9_d6), ._7(_8_digit_display_9__7),
    .D7(_8_digit_display_9_d7));
  RV32I_Instruction_Display rv32i_instruction_display_4 (
    .INSTR(INSTR_WRITE), ._0(rv32i_instruction_display_4__0), .D0(rv32i_instruction_display_4_d0),
    ._1(rv32i_instruction_display_4__1), .D1(rv32i_instruction_display_4_d1),
    ._2(rv32i_instruction_display_4__2), .D2(rv32i_instruction_display_4_d2),
    ._3(rv32i_instruction_display_4__3), .D3(rv32i_instruction_display_4_d3),
    ._4(rv32i_instruction_display_4__4), .D4(rv32i_instruction_display_4_d4),
    ._5(rv32i_instruction_display_4__5), .D5(rv32i_instruction_display_4_d5),
    ._6(rv32i_instruction_display_4__6), .D6(rv32i_instruction_display_4_d6),
    ._7(rv32i_instruction_display_4__7), .D7(rv32i_instruction_display_4_d7));
  Seven_Seg_Hex seven_seg_hex_90 (.d(_8_digit_display_9__3), .dp(_8_digit_display_9_d3));
  Seven_Seg_Hex seven_seg_hex_91 (.d(_8_digit_display_9__4), .dp(_8_digit_display_9_d4));
  SixteenSeg sixteenseg_28 (.led(rv32i_instruction_display_4__3), .dp(rv32i_instruction_display_4_d3));
  SixteenSeg sixteenseg_29 (.led(rv32i_instruction_display_4__4), .dp(rv32i_instruction_display_4_d4));
  RV32I CPU (
    .CLC(CLC), .INSTR(INSTR_DECODE), .NORMAL(NORMAL), .RUN(RUN), .CPU_HOLD(1'b0), .MEM_R(MEM_R_W),
    .INSTR_EXECUTE(INSTR_EXECUTE), .INSTR_MEMORY(INSTR_MEMORY), .INSTR_WRITE(INSTR_WRITE), .GO(GO),
    .HELD_REGISTER_0(HELD_REGISTER_0), .HELD_REGISTER_1(HELD_REGISTER_1), .ALU_INSTR(ALU_INSTR),
    .ALU_A(ALU_A), .ALU_B(ALU_B), .ALU_Y(ALU_Y), .COMP(COMP), .PC(PC_OUT),
    .CPU_SET_MEM_ADDRESS(CPU_cpu_set_mem_address), .MEM_ADDRESS(CPU_mem_address),
    .CPU_WRITE_MEM(CPU_cpu_write_mem), .MEM_W(CPU_mem_w), .ERROR(CPU_error));
  Seven_Seg_Hex seven_seg_hex_92 (.d(_8_digit_display_9__5), .dp(_8_digit_display_9_d5));
  Seven_Seg_Hex seven_seg_hex_93 (.d(_8_digit_display_9__6), .dp(_8_digit_display_9_d6));
  SixteenSeg sixteenseg_30 (.led(rv32i_instruction_display_4__5), .dp(rv32i_instruction_display_4_d5));
  SixteenSeg sixteenseg_31 (.led(rv32i_instruction_display_4__6), .dp(rv32i_instruction_display_4_d6));
  Seven_Seg_Hex seven_seg_hex_94 (.d(_8_digit_display_9__7), .dp(_8_digit_display_9_d7));
  SixteenSeg sixteenseg_32 (.led(rv32i_instruction_display_4__7), .dp(rv32i_instruction_display_4_d7));
  Break break_1 (.brk(CPU_error));

  // Other names for the same wires on the sheet: ROM_A[23:0] = BOOT_CNT

  // Notes on the sheet:
  //   CLC: Hz: 10
  //   ROM
  //   NORMAL
  //   RUN
  //   GO
  //   PROGRAM LENGTH
  //   contents of ROM (hex, n*v repeats v):
  //   140006f,0,aaaaaaaa,0,0,0,0,0,0,0,0,0,0,0,0,0,0,0,0,0,0,0,0,0,0,0,0,0,0,0,0,0,0,0,
  //   0,0,0,0,0,0,1437,0,497,0,40848533,0,409405b3,0,b57633,0,b566b3,0,b54733,0,1341793,
  //   0,c55813,0,40b7d893,0,fff7c913,0,ffb97993,0,57ea13,0,ca1ab3,0,ca5b33,0,40ca5bb3,0,
  //   17b2c33,0,16bacb3,0,17b3d33,0,16bbdb3,0,bae13,0,b2e93,0,bbf13,0,263f93,0,13,0,13,
  //   0,13,0,0,0,100103,0,200123,0,2011a3,0,104103,0,200223,0,2012a3,0,111003,0,201323,
  //   0,2023a3,0,105103,0,201423,0,2024a3,0,0,0,13,0,fffff06f
  //   DECODE
  //   ADD ALU INSTRUCTION DECODER HERE
  //   EXECUTE
  //   MEM R/W
  //   MEMORY
  //   ADD VALUE GOING INTO REGISTER AND REGISTER # HERE
  //   WRITE
  //   ADD REGISTERS HERE
endmodule
