// Digital circuit RV32I-Write-Control.dig as structural Verilog
module RV32I_Write_Control (
  input  [31:0] INSTR,
  input  Normal,
  input  Run,
  input  Comp,
  output EXECUTE_HOLD,
  output REG_WRITE,
  output ALU_SET_REGISTER,
  output ALU_SET_PC,
  output ALU_SET_MEM_R_W_A,
  output WRITE_TO_MEMORY
);

  wire and_2_out, rv32i_instruction_decoder_1_p2, rv32i_instruction_decoder_1_p4;
  wire [3:1] rv32i_instruction_decoder_1_p3;

  // RV32I_Instruction_Decoder rv32i_instruction_decoder_1: pin names not known; wires that end beside it: INSTR, rv32i_instruction_decoder_1_p2, {rv32i_instruction_decoder_1_p3, ALU_SET_REGISTER}, rv32i_instruction_decoder_1_p4
  and and_1 (EXECUTE_HOLD, ~INSTR[4], INSTR[5], INSTR[6]);  // And
  and and_2 (and_2_out, Comp, rv32i_instruction_decoder_1_p3[2]);
  and and_3 (REG_WRITE, rv32i_instruction_decoder_1_p2, Normal, Run);
  and and_4 (ALU_SET_MEM_R_W_A, rv32i_instruction_decoder_1_p3[3], Normal);
  and and_5 (WRITE_TO_MEMORY, rv32i_instruction_decoder_1_p3[3], rv32i_instruction_decoder_1_p4, Normal);
  or or_1 (ALU_SET_PC, rv32i_instruction_decoder_1_p3[1], and_2_out);
endmodule
