// Digital circuit RV32I-Write-Instruction-Decoder.dig as structural Verilog
module RV32I_Write_Instruction_Decoder (
  input  [31:0] IN,
  output REG_HOLD
);

  wire nand_1_out;

  nand nand_1 (nand_1_out, ~IN[2], ~IN[3], ~IN[4], IN[5]);  // NAnd
  and and_1 (REG_HOLD, IN[0], IN[1], nand_1_out);

  // Notes on the sheet:
  //   IN: default 20191123
  //   Write to Register
endmodule
